// Logisim project TOY16_FINAL.circ as structural Verilog: 52 circuits, main circuit MACHINE16
module MACHINE16 (
  output halt,
  output [7:0] PC
);

  wire alu16b_1_pos, alu16b_1_zero, and_1_out, and_2_out, and_3_out, and_4_out, and_5_out, clock_1_out,
       control16_1_alu_b_mux, control16_1_aop0, control16_1_aop1, control16_1_aop2, control16_1_is_halt,
       control16_1_mem_write, control16_1_memaddr_ir, control16_1_memaddr_rt, control16_1_pc_load,
       control16_1_pc_src_rd, control16_1_read_rd_mux, control16_1_reg_write, control16_1_regsrc_mem,
       control16_1_regsrc_pc, control16_1_rs_sel_d, not_1_out, or_1_out, or_2_out, phasegen_1_e,
       phasegen_1_ew, phasegen_1_fw, register_1_q, undriven, undriven_2;
  wire [3:0] mux2_4_1_y, register_2_q, register_2_q_2, register_2_q_3, register_2_q_4, undriven_6;
  wire [7:0] mux2_8_1_y, mux2_8_2_y, regfile_1_rtd, undriven_4, undriven_5;
  wire [15:0] alu16b_1_r, MAIN_dout, mux2_16_1_y, mux2_16_2_y, mux2_16_3_y, regfile_1_rsd;
  wire [15:8] regfile_1_rtd_2, undriven_3;

  Clock clock_1 (.out(clock_1_out));
  and and_1 (and_1_out, control16_1_is_halt, or_2_out);
  PHASEGEN phasegen_1 (.CLK(clock_1_out), .FW(phasegen_1_fw), .E(phasegen_1_e), .EW(phasegen_1_ew));  // open: F
  not not_1 (not_1_out, halt);
  or or_1 (or_1_out, register_1_q, and_1_out);
  or or_2 (or_2_out, phasegen_1_e, phasegen_1_ew);
  and and_2 (and_2_out, phasegen_1_fw, not_1_out);
  and and_3 (and_3_out, control16_1_pc_load, not_1_out);
  and and_4 (and_4_out, control16_1_reg_write, not_1_out);
  and and_5 (and_5_out, control16_1_mem_write, not_1_out);
  Register #(.width(1), .trigger("rising")) register_1 (
    .D(or_1_out), .en(1'b1), .clk(clock_1_out), .Q(register_1_q), .clr(1'b0));
  PC8 pc8_1 (
    .ADDR({register_2_q_4, register_2_q_3}), .RD(regfile_1_rtd), .PC_LOAD(and_3_out),
    .PC_SRC_RD(control16_1_pc_src_rd), .FETCH_WR(undriven_2), .CLK(undriven), .PC(PC));
  RAM #(.addrWidth(8), .dataWidth(16), .enables("line"), .trigger("high"), .databus("bibus")) MAIN (
    .addr(mux2_8_2_y), .we(and_5_out), .clk(1'b1), .din(regfile_1_rsd), .dout(MAIN_dout));
  MUX2_8 mux2_8_1 (.A(PC), .B(undriven_4), .SEL(control16_1_memaddr_rt), .Y(mux2_8_1_y));
  Register #(.width(16), .trigger("rising")) register_2 (
    .D(MAIN_dout), .en(and_2_out), .clk(clock_1_out),
    .Q({register_2_q_2, register_2_q, register_2_q_4, register_2_q_3}), .clr(1'b0));
  MUX2_8 mux2_8_2 (.A(mux2_8_1_y), .B(undriven_5), .SEL(control16_1_memaddr_ir), .Y(mux2_8_2_y));
  CONTROL16 control16_1 (
    .OP(register_2_q_2), .EXEC(or_2_out), .EXWR(phasegen_1_ew), .ZERO(alu16b_1_zero), .POS(alu16b_1_pos),
    .AOP0(control16_1_aop0), .AOP1(control16_1_aop1), .AOP2(control16_1_aop2),
    .ALU_B_MUX(control16_1_alu_b_mux), .MEMADDR_IR(control16_1_memaddr_ir),
    .MEMADDR_RT(control16_1_memaddr_rt), .MEM_WRITE(control16_1_mem_write),
    .REG_WRITE(control16_1_reg_write), .REGSRC_MEM(control16_1_regsrc_mem),
    .REGSRC_PC(control16_1_regsrc_pc), .READ_RD_MUX(control16_1_read_rd_mux), .PC_LOAD(control16_1_pc_load),
    .PC_SRC_RD(control16_1_pc_src_rd), .RS_SEL_D(control16_1_rs_sel_d), .IS_HALT(control16_1_is_halt));
  MUX2_4 mux2_4_1 (.A(register_2_q_4), .B(register_2_q), .SEL(control16_1_rs_sel_d), .Y(mux2_4_1_y));
  REGFILE regfile_1 (
    .RS(mux2_4_1_y), .RT(register_2_q_3), .RD(undriven_6), .WD(mux2_16_2_y), .RegWrite(and_4_out),
    .ReadRdMux(control16_1_read_rd_mux), .CLK(clock_1_out), .RSD(regfile_1_rsd),
    .RTD({regfile_1_rtd_2, regfile_1_rtd}));
  MUX2_16 mux2_16_1 (.A(alu16b_1_r), .B({undriven_3, PC}), .SEL(control16_1_regsrc_pc), .Y(mux2_16_1_y));
  MUX2_16 mux2_16_2 (.A(mux2_16_1_y), .B(MAIN_dout), .SEL(control16_1_regsrc_mem), .Y(mux2_16_2_y));
  MUX2_16 mux2_16_3 (
    .A({regfile_1_rtd_2, regfile_1_rtd}), .B({{8{1'b0}}, register_2_q_4, register_2_q_3}),
    .SEL(control16_1_alu_b_mux), .Y(mux2_16_3_y));
  ALU16B alu16b_1 (
    .A(regfile_1_rsd), .B(mux2_16_3_y), .OP0(control16_1_aop0), .OP1(control16_1_aop1),
    .OP2(control16_1_aop2), .R(alu16b_1_r), .Zero(alu16b_1_zero), .Pos(alu16b_1_pos));

  // Notes on the sheet:
  //   Ahmad Hussain 33440
endmodule

module CONTROL16 (
  input  EXEC,
  input  [3:0] OP,
  input  EXWR,
  input  ZERO,
  input  POS,
  output AOP0,
  output AOP1,
  output AOP2,
  output ALU_B_MUX,
  output MEMADDR_IR,
  output MEMADDR_RT,
  output MEM_WRITE,
  output REG_WRITE,
  output REGSRC_MEM,
  output REGSRC_PC,
  output READ_RD_MUX,
  output PC_LOAD,
  output PC_SRC_RD,
  output RS_SEL_D,
  output IS_HALT
);

  wire and_14_out, and_15_out, decoder4b_1_d1, decoder4b_1_d2, decoder4b_1_d3, decoder4b_1_d4,
       decoder4b_1_d5, decoder4b_1_d6, decoder4b_1_d7, decoder4b_1_d8, decoder4b_1_d9, decoder4b_1_d10,
       decoder4b_1_d11, decoder4b_1_d12, decoder4b_1_d13, decoder4b_1_d14, decoder4b_1_d15, not_1_out,
       not_2_out, not_3_out, not_4_out, not_5_out, not_6_out, or_1_out, or_2_out, or_3_out, or_4_out,
       or_5_out, or_6_out, or_7_out, or_8_out, or_9_out, or_10_out, or_11_out, or_12_out, or_13_out,
       or_14_out, or_15_out, or_16_out, or_17_out, or_18_out, or_19_out, or_20_out, or_21_out, or_22_out,
       or_23_out, or_24_out, or_25_out, or_26_out, or_27_out, or_28_out, or_29_out, or_30_out, undriven,
       undriven_2, undriven_3, undriven_4, undriven_5, undriven_6, undriven_7, undriven_8, undriven_9,
       undriven_10, undriven_11, undriven_12, undriven_13, undriven_14, undriven_15, undriven_16,
       undriven_17, undriven_18;

  DECODER4B decoder4b_1 (
    .S0(undriven), .S1(undriven_2), .S2(undriven_3), .S3(undriven_4), .D0(IS_HALT), .D1(decoder4b_1_d1),
    .D2(decoder4b_1_d2), .D3(decoder4b_1_d3), .D4(decoder4b_1_d4), .D5(decoder4b_1_d5), .D6(decoder4b_1_d6),
    .D7(decoder4b_1_d7), .D8(decoder4b_1_d8), .D9(decoder4b_1_d9), .D10(decoder4b_1_d10),
    .D11(decoder4b_1_d11), .D12(decoder4b_1_d12), .D13(decoder4b_1_d13), .D14(decoder4b_1_d14),
    .D15(decoder4b_1_d15));
  or or_1 (or_1_out, decoder4b_1_d1, decoder4b_1_d2);
  or or_2 (or_2_out, or_1_out, decoder4b_1_d3);
  or or_3 (or_3_out, or_2_out, decoder4b_1_d4);
  or or_4 (or_4_out, or_3_out, decoder4b_1_d5);
  or or_5 (or_5_out, or_4_out, decoder4b_1_d6);
  or or_6 (or_6_out, or_5_out, decoder4b_1_d7);
  or or_7 (or_7_out, or_6_out, decoder4b_1_d8);
  or or_8 (or_8_out, or_7_out, decoder4b_1_d10);
  or or_9 (or_9_out, or_8_out, decoder4b_1_d15);
  or or_10 (or_10_out, decoder4b_1_d9, decoder4b_1_d11);
  not not_1 (not_1_out, decoder4b_1_d7);
  not not_2 (not_2_out, not_1_out);
  or or_11 (or_11_out, undriven_9, decoder4b_1_d8);
  or or_12 (or_12_out, or_11_out, undriven_8);
  or or_13 (or_13_out, decoder4b_1_d10, decoder4b_1_d11);
  or or_14 (or_14_out, decoder4b_1_d8, decoder4b_1_d10);
  not not_3 (not_3_out, decoder4b_1_d15);
  not not_4 (not_4_out, not_3_out);
  or or_15 (or_15_out, decoder4b_1_d12, decoder4b_1_d13);
  or or_16 (or_16_out, or_15_out, decoder4b_1_d14);
  or or_17 (or_17_out, undriven_6, decoder4b_1_d4);
  or or_18 (or_18_out, or_17_out, decoder4b_1_d6);
  or or_19 (or_19_out, undriven_7, decoder4b_1_d4);
  or or_20 (or_20_out, or_19_out, undriven_11);
  or or_21 (or_21_out, or_20_out, undriven_14);
  or or_22 (or_22_out, or_21_out, undriven_13);
  or or_23 (or_23_out, undriven_5, undriven_15);
  or or_24 (or_24_out, or_23_out, undriven_11);
  or or_25 (or_25_out, or_24_out, undriven_16);
  or or_26 (or_26_out, or_25_out, undriven_17);
  not not_5 (not_5_out, undriven_12);
  not not_6 (not_6_out, not_5_out);
  or or_27 (or_27_out, undriven_10, decoder4b_1_d11);
  and and_1 (ALU_B_MUX, not_2_out, EXEC);
  and and_2 (MEMADDR_IR, or_12_out, EXEC);
  and and_3 (MEMADDR_RT, or_13_out, EXEC);
  and and_4 (REGSRC_MEM, or_14_out, EXEC);
  and and_5 (REGSRC_PC, not_4_out, EXEC);
  and and_6 (READ_RD_MUX, or_16_out, EXEC);
  and and_7 (AOP0, or_18_out, EXEC);
  and and_8 (AOP1, or_22_out, EXEC);
  and and_9 (AOP2, or_26_out, EXEC);
  and and_10 (PC_SRC_RD, not_6_out, EXEC);
  and and_11 (RS_SEL_D, or_27_out, EXEC);
  and and_12 (REG_WRITE, or_9_out, EXWR);
  and and_13 (MEM_WRITE, or_10_out, EXWR);
  and and_14 (and_14_out, undriven_16, ZERO);
  and and_15 (and_15_out, undriven_17, POS);
  or or_28 (or_28_out, and_14_out, and_15_out);
  or or_29 (or_29_out, or_28_out, undriven_18);
  or or_30 (or_30_out, or_29_out, decoder4b_1_d15);
  and and_16 (PC_LOAD, or_30_out, EXWR);
endmodule

module REGFILE (
  input  [3:0] RS,
  input  [3:0] RT,
  input  [3:0] RD,
  input  RegWrite,
  input  ReadRdMux,
  input  CLK,
  input  [15:0] WD,
  output [15:0] RSD,
  output [15:0] RTD
);

  wire and_1_out, and_2_out, and_3_out, and_4_out, and_5_out, and_6_out, and_7_out, and_8_out, and_9_out,
       and_10_out, and_11_out, and_12_out, and_13_out, and_14_out, and_15_out, busmux2b_1_y0, busmux2b_1_y1,
       busmux2b_1_y2, busmux2b_1_y3, decoder4b_1_d1, decoder4b_1_d2, decoder4b_1_d3, decoder4b_1_d4,
       decoder4b_1_d5, decoder4b_1_d6, decoder4b_1_d7, decoder4b_1_d8, decoder4b_1_d9, decoder4b_1_d10,
       decoder4b_1_d11, decoder4b_1_d12, decoder4b_1_d13, decoder4b_1_d14, decoder4b_1_d15, not_1_out,
       undriven, undriven_2, undriven_3, undriven_4, undriven_5, undriven_6, undriven_7, undriven_8,
       undriven_9, undriven_10, undriven_11, undriven_12, undriven_14, undriven_15, undriven_16, undriven_17,
       undriven_20;
  wire [15:0] and_16_out, and_17_out, and_18_out, and_19_out, and_20_out, and_21_out, and_22_out, and_23_out,
       and_24_out, and_25_out, and_26_out, and_27_out, and_28_out, and_29_out, and_30_out, and_31_out,
       and_32_out, and_33_out, and_34_out, and_35_out, and_36_out, and_37_out, and_38_out, and_39_out,
       and_40_out, and_41_out, and_42_out, and_43_out, and_44_out, and_45_out, and_46_out, and_47_out,
       or_1_out, or_2_out, or_3_out, or_4_out, or_5_out, or_6_out, or_7_out, or_8_out, or_9_out, or_10_out,
       or_11_out, or_12_out, or_13_out, or_14_out, or_16_out, or_17_out, or_18_out, or_19_out, or_20_out,
       or_21_out, or_22_out, or_23_out, or_24_out, or_25_out, or_26_out, or_27_out, or_28_out, or_29_out,
       or_30_out, register_1_q, register_2_q, register_3_q, register_4_q, register_5_q, register_6_q,
       register_7_q, register_8_q, register_9_q, register_10_q, register_11_q, register_12_q, register_13_q,
       register_14_q, register_15_q, undriven_13, undriven_18, undriven_19, undriven_21;
  wire [15:15] decoder4b_2_d0, decoder4b_2_d1, decoder4b_2_d2, decoder4b_2_d3, decoder4b_2_d4,
       decoder4b_2_d5, decoder4b_2_d6, decoder4b_2_d7, decoder4b_2_d8, decoder4b_2_d9, decoder4b_2_d10,
       decoder4b_2_d11, decoder4b_2_d12, decoder4b_2_d13, decoder4b_2_d14, decoder4b_2_d15, decoder4b_3_d0,
       decoder4b_3_d1, decoder4b_3_d2, decoder4b_3_d3, decoder4b_3_d4, decoder4b_3_d5, decoder4b_3_d6,
       decoder4b_3_d7, decoder4b_3_d8, decoder4b_3_d9, decoder4b_3_d10, decoder4b_3_d11, decoder4b_3_d12,
       decoder4b_3_d13, decoder4b_3_d14, decoder4b_3_d15;

  not not_1 (not_1_out, ReadRdMux);
  DECODER4B decoder4b_1 (
    .S0(undriven_9), .S1(undriven_10), .S2(undriven_11), .S3(undriven_12), .D1(decoder4b_1_d1),
    .D2(decoder4b_1_d2), .D3(decoder4b_1_d3), .D4(decoder4b_1_d4), .D5(decoder4b_1_d5), .D6(decoder4b_1_d6),
    .D7(decoder4b_1_d7), .D8(decoder4b_1_d8), .D9(decoder4b_1_d9), .D10(decoder4b_1_d10),
    .D11(decoder4b_1_d11), .D12(decoder4b_1_d12), .D13(decoder4b_1_d13), .D14(decoder4b_1_d14),
    .D15(decoder4b_1_d15));  // open: D0
  BUSMUX2B busmux2b_1 (
    .a0(undriven_5), .a1(undriven_6), .a2(undriven_7), .a3(undriven_8), .b0(undriven_16), .b1(undriven_15),
    .b2(undriven_17), .b3(undriven_14), .sA(not_1_out), .sB(ReadRdMux), .y0(busmux2b_1_y0),
    .y1(busmux2b_1_y1), .y2(busmux2b_1_y2), .y3(busmux2b_1_y3));
  and and_1 (and_1_out, decoder4b_1_d1, RegWrite);
  and and_2 (and_2_out, decoder4b_1_d2, RegWrite);
  and and_3 (and_3_out, decoder4b_1_d3, RegWrite);
  and and_4 (and_4_out, decoder4b_1_d4, RegWrite);
  and and_5 (and_5_out, decoder4b_1_d5, RegWrite);
  and and_6 (and_6_out, decoder4b_1_d6, RegWrite);
  and and_7 (and_7_out, decoder4b_1_d7, RegWrite);
  and and_8 (and_8_out, decoder4b_1_d8, RegWrite);
  and and_9 (and_9_out, decoder4b_1_d9, RegWrite);
  and and_10 (and_10_out, decoder4b_1_d10, RegWrite);
  and and_11 (and_11_out, decoder4b_1_d11, RegWrite);
  and and_12 (and_12_out, decoder4b_1_d12, RegWrite);
  and and_13 (and_13_out, decoder4b_1_d13, RegWrite);
  and and_14 (and_14_out, decoder4b_1_d14, RegWrite);
  and and_15 (and_15_out, decoder4b_1_d15, RegWrite);
  Register #(.width(16), .trigger("rising")) register_1 (
    .D(undriven_13), .en(and_1_out), .clk(CLK), .Q(register_1_q), .clr(1'b0));
  Register #(.width(16), .trigger("rising")) register_2 (
    .D(undriven_18), .en(and_2_out), .clk(undriven_20), .Q(register_2_q), .clr(1'b0));
  Register #(.width(16), .trigger("rising")) register_3 (
    .D(undriven_19), .en(and_3_out), .clk(undriven_20), .Q(register_3_q), .clr(1'b0));
  Register #(.width(16), .trigger("rising")) register_4 (
    .D(undriven_19), .en(and_4_out), .clk(undriven_20), .Q(register_4_q), .clr(1'b0));
  Register #(.width(16), .trigger("rising")) register_5 (
    .D(undriven_19), .en(and_5_out), .clk(undriven_20), .Q(register_5_q), .clr(1'b0));
  Register #(.width(16), .trigger("rising")) register_6 (
    .D(undriven_19), .en(and_6_out), .clk(undriven_20), .Q(register_6_q), .clr(1'b0));
  Register #(.width(16), .trigger("rising")) register_7 (
    .D(undriven_19), .en(and_7_out), .clk(undriven_20), .Q(register_7_q), .clr(1'b0));
  Register #(.width(16), .trigger("rising")) register_8 (
    .D(undriven_19), .en(and_8_out), .clk(undriven_20), .Q(register_8_q), .clr(1'b0));
  Register #(.width(16), .trigger("rising")) register_9 (
    .D(undriven_19), .en(and_9_out), .clk(undriven_20), .Q(register_9_q), .clr(1'b0));
  Register #(.width(16), .trigger("rising")) register_10 (
    .D(undriven_19), .en(and_10_out), .clk(undriven_20), .Q(register_10_q), .clr(1'b0));
  Register #(.width(16), .trigger("rising")) register_11 (
    .D(undriven_19), .en(and_11_out), .clk(undriven_20), .Q(register_11_q), .clr(1'b0));
  Register #(.width(16), .trigger("rising")) register_12 (
    .D(undriven_19), .en(and_12_out), .clk(undriven_20), .Q(register_12_q), .clr(1'b0));
  Register #(.width(16), .trigger("rising")) register_13 (
    .D(undriven_19), .en(and_13_out), .clk(undriven_20), .Q(register_13_q), .clr(1'b0));
  Register #(.width(16), .trigger("rising")) register_14 (
    .D(undriven_19), .en(and_14_out), .clk(undriven_20), .Q(register_14_q), .clr(1'b0));
  Register #(.width(16), .trigger("rising")) register_15 (
    .D(undriven_19), .en(and_15_out), .clk(undriven_20), .Q(register_15_q), .clr(1'b0));
  DECODER4B decoder4b_2 (
    .S0(undriven), .S1(undriven_2), .S2(undriven_3), .S3(undriven_4), .D0(decoder4b_2_d0[15]),
    .D1(decoder4b_2_d1[15]), .D2(decoder4b_2_d2[15]), .D3(decoder4b_2_d3[15]), .D4(decoder4b_2_d4[15]),
    .D5(decoder4b_2_d5[15]), .D6(decoder4b_2_d6[15]), .D7(decoder4b_2_d7[15]), .D8(decoder4b_2_d8[15]),
    .D9(decoder4b_2_d9[15]), .D10(decoder4b_2_d10[15]), .D11(decoder4b_2_d11[15]), .D12(decoder4b_2_d12[15]),
    .D13(decoder4b_2_d13[15]), .D14(decoder4b_2_d14[15]), .D15(decoder4b_2_d15[15]));
  assign and_16_out = {16{1'b0}} & {16{decoder4b_2_d0[15]}};  // AND_Gate and_16, 16 bits wide
  assign and_17_out = register_1_q & {16{decoder4b_2_d1[15]}};  // AND_Gate and_17, 16 bits wide
  assign and_18_out = register_2_q & {16{decoder4b_2_d2[15]}};  // AND_Gate and_18, 16 bits wide
  assign and_19_out = register_3_q & {16{decoder4b_2_d3[15]}};  // AND_Gate and_19, 16 bits wide
  assign and_20_out = register_4_q & {16{decoder4b_2_d4[15]}};  // AND_Gate and_20, 16 bits wide
  assign and_21_out = register_5_q & {16{decoder4b_2_d5[15]}};  // AND_Gate and_21, 16 bits wide
  assign and_22_out = register_6_q & {16{decoder4b_2_d6[15]}};  // AND_Gate and_22, 16 bits wide
  assign and_23_out = register_7_q & {16{decoder4b_2_d7[15]}};  // AND_Gate and_23, 16 bits wide
  assign and_24_out = register_8_q & {16{decoder4b_2_d8[15]}};  // AND_Gate and_24, 16 bits wide
  assign and_25_out = register_9_q & {16{decoder4b_2_d9[15]}};  // AND_Gate and_25, 16 bits wide
  assign and_26_out = register_10_q & {16{decoder4b_2_d10[15]}};  // AND_Gate and_26, 16 bits wide
  assign and_27_out = register_11_q & {16{decoder4b_2_d11[15]}};  // AND_Gate and_27, 16 bits wide
  assign and_28_out = register_12_q & {16{decoder4b_2_d12[15]}};  // AND_Gate and_28, 16 bits wide
  assign and_29_out = register_13_q & {16{decoder4b_2_d13[15]}};  // AND_Gate and_29, 16 bits wide
  assign and_30_out = register_14_q & {16{decoder4b_2_d14[15]}};  // AND_Gate and_30, 16 bits wide
  assign and_31_out = register_15_q & {16{decoder4b_2_d15[15]}};  // AND_Gate and_31, 16 bits wide
  assign or_1_out = and_16_out | and_17_out;  // OR_Gate or_1, 16 bits wide
  assign or_2_out = or_1_out | and_18_out;  // OR_Gate or_2, 16 bits wide
  assign or_3_out = or_2_out | and_19_out;  // OR_Gate or_3, 16 bits wide
  assign or_4_out = or_3_out | and_20_out;  // OR_Gate or_4, 16 bits wide
  assign or_5_out = or_4_out | and_21_out;  // OR_Gate or_5, 16 bits wide
  assign or_6_out = or_5_out | and_22_out;  // OR_Gate or_6, 16 bits wide
  assign or_7_out = or_6_out | and_23_out;  // OR_Gate or_7, 16 bits wide
  assign or_8_out = or_7_out | and_24_out;  // OR_Gate or_8, 16 bits wide
  assign or_9_out = or_8_out | and_25_out;  // OR_Gate or_9, 16 bits wide
  assign or_10_out = or_9_out | and_26_out;  // OR_Gate or_10, 16 bits wide
  assign or_11_out = or_10_out | and_27_out;  // OR_Gate or_11, 16 bits wide
  assign or_12_out = or_11_out | and_28_out;  // OR_Gate or_12, 16 bits wide
  assign or_13_out = or_12_out | and_29_out;  // OR_Gate or_13, 16 bits wide
  assign or_14_out = or_13_out | and_30_out;  // OR_Gate or_14, 16 bits wide
  assign RSD = or_14_out | and_31_out;  // OR_Gate or_15, 16 bits wide
  DECODER4B decoder4b_3 (
    .S0(busmux2b_1_y0), .S1(busmux2b_1_y1), .S2(busmux2b_1_y2), .S3(busmux2b_1_y3), .D0(decoder4b_3_d0[15]),
    .D1(decoder4b_3_d1[15]), .D2(decoder4b_3_d2[15]), .D3(decoder4b_3_d3[15]), .D4(decoder4b_3_d4[15]),
    .D5(decoder4b_3_d5[15]), .D6(decoder4b_3_d6[15]), .D7(decoder4b_3_d7[15]), .D8(decoder4b_3_d8[15]),
    .D9(decoder4b_3_d9[15]), .D10(decoder4b_3_d10[15]), .D11(decoder4b_3_d11[15]), .D12(decoder4b_3_d12[15]),
    .D13(decoder4b_3_d13[15]), .D14(decoder4b_3_d14[15]), .D15(decoder4b_3_d15[15]));
  assign and_32_out = undriven_21 & {16{decoder4b_3_d0[15]}};  // AND_Gate and_32, 16 bits wide
  assign and_33_out = register_1_q & {16{decoder4b_3_d1[15]}};  // AND_Gate and_33, 16 bits wide
  assign and_34_out = register_2_q & {16{decoder4b_3_d2[15]}};  // AND_Gate and_34, 16 bits wide
  assign and_35_out = register_3_q & {16{decoder4b_3_d3[15]}};  // AND_Gate and_35, 16 bits wide
  assign and_36_out = register_4_q & {16{decoder4b_3_d4[15]}};  // AND_Gate and_36, 16 bits wide
  assign and_37_out = register_5_q & {16{decoder4b_3_d5[15]}};  // AND_Gate and_37, 16 bits wide
  assign and_38_out = register_6_q & {16{decoder4b_3_d6[15]}};  // AND_Gate and_38, 16 bits wide
  assign and_39_out = register_7_q & {16{decoder4b_3_d7[15]}};  // AND_Gate and_39, 16 bits wide
  assign and_40_out = register_8_q & {16{decoder4b_3_d8[15]}};  // AND_Gate and_40, 16 bits wide
  assign and_41_out = register_9_q & {16{decoder4b_3_d9[15]}};  // AND_Gate and_41, 16 bits wide
  assign and_42_out = register_10_q & {16{decoder4b_3_d10[15]}};  // AND_Gate and_42, 16 bits wide
  assign and_43_out = register_11_q & {16{decoder4b_3_d11[15]}};  // AND_Gate and_43, 16 bits wide
  assign and_44_out = register_12_q & {16{decoder4b_3_d12[15]}};  // AND_Gate and_44, 16 bits wide
  assign and_45_out = register_13_q & {16{decoder4b_3_d13[15]}};  // AND_Gate and_45, 16 bits wide
  assign and_46_out = register_14_q & {16{decoder4b_3_d14[15]}};  // AND_Gate and_46, 16 bits wide
  assign and_47_out = register_15_q & {16{decoder4b_3_d15[15]}};  // AND_Gate and_47, 16 bits wide
  assign or_16_out = and_32_out | and_33_out;  // OR_Gate or_16, 16 bits wide
  assign or_17_out = or_16_out | and_34_out;  // OR_Gate or_17, 16 bits wide
  assign or_18_out = or_17_out | and_35_out;  // OR_Gate or_18, 16 bits wide
  assign or_19_out = or_18_out | and_36_out;  // OR_Gate or_19, 16 bits wide
  assign or_20_out = or_19_out | and_37_out;  // OR_Gate or_20, 16 bits wide
  assign or_21_out = or_20_out | and_38_out;  // OR_Gate or_21, 16 bits wide
  assign or_22_out = or_21_out | and_39_out;  // OR_Gate or_22, 16 bits wide
  assign or_23_out = or_22_out | and_40_out;  // OR_Gate or_23, 16 bits wide
  assign or_24_out = or_23_out | and_41_out;  // OR_Gate or_24, 16 bits wide
  assign or_25_out = or_24_out | and_42_out;  // OR_Gate or_25, 16 bits wide
  assign or_26_out = or_25_out | and_43_out;  // OR_Gate or_26, 16 bits wide
  assign or_27_out = or_26_out | and_44_out;  // OR_Gate or_27, 16 bits wide
  assign or_28_out = or_27_out | and_45_out;  // OR_Gate or_28, 16 bits wide
  assign or_29_out = or_28_out | and_46_out;  // OR_Gate or_29, 16 bits wide
  assign or_30_out = or_29_out | and_47_out;  // OR_Gate or_30, 16 bits wide
endmodule

module PC8 (
  input  [7:0] ADDR,
  input  PC_LOAD,
  input  PC_SRC_RD,
  input  FETCH_WR,
  input  CLK,
  input  [7:0] RD,
  output [7:0] PC
);

  wire and_1_out, and_2_out, and_3_out, and_4_out, and_5_out, and_6_out, and_7_out, and_8_out, and_9_out,
       and_10_out, and_11_out, and_12_out, and_13_out, and_14_out, and_15_out, and_16_out, and_17_out,
       and_18_out, and_19_out, and_20_out, and_21_out, and_22_out, and_23_out, and_24_out, and_25_out,
       and_26_out, and_27_out, and_28_out, and_29_out, and_30_out, and_31_out, and_32_out, inc8_1_s0,
       inc8_1_s1, inc8_1_s2, inc8_1_s3, inc8_1_s4, inc8_1_s5, inc8_1_s6, inc8_1_s7, not_1_out, not_2_out,
       or_1_out, or_2_out, or_3_out, or_4_out, or_5_out, or_6_out, or_7_out, or_8_out, or_17_out, undriven,
       undriven_2, undriven_3, undriven_4, undriven_5, undriven_6, undriven_7, undriven_8, undriven_9,
       undriven_10, undriven_11, undriven_12, undriven_13, undriven_14, undriven_15, undriven_16,
       undriven_17, undriven_18, undriven_19, undriven_20, undriven_21, undriven_22, undriven_23,
       undriven_24, undriven_25;
  wire [7:0] or_9_out;

  Register #(.width(8), .trigger("rising")) register_1 (.D(or_9_out), .en(or_17_out), .clk(CLK), .Q(PC), .clr(1'b0));
  INC8 inc8_1 (
    .A0(undriven_18), .A1(undriven_19), .A2(undriven_17), .A3(undriven_20), .A4(undriven_21),
    .A5(undriven_16), .A6(undriven_22), .A7(undriven_23), .S0(inc8_1_s0), .S1(inc8_1_s1), .S2(inc8_1_s2),
    .S3(inc8_1_s3), .S4(inc8_1_s4), .S5(inc8_1_s5), .S6(inc8_1_s6), .S7(inc8_1_s7));  // open: Cout
  not not_1 (not_1_out, PC_SRC_RD);
  and and_1 (and_1_out, ADDR[0], not_1_out);
  and and_2 (and_2_out, undriven, not_1_out);
  and and_3 (and_3_out, undriven_2, not_1_out);
  and and_4 (and_4_out, undriven_3, not_1_out);
  and and_5 (and_5_out, undriven_4, not_1_out);
  and and_6 (and_6_out, undriven_5, not_1_out);
  and and_7 (and_7_out, undriven_6, not_1_out);
  and and_8 (and_8_out, undriven_7, not_1_out);
  and and_9 (and_9_out, undriven_8, PC_SRC_RD);
  and and_10 (and_10_out, undriven_9, undriven_24);
  and and_11 (and_11_out, undriven_10, undriven_24);
  and and_12 (and_12_out, undriven_11, undriven_24);
  and and_13 (and_13_out, undriven_12, undriven_24);
  and and_14 (and_14_out, undriven_13, undriven_24);
  and and_15 (and_15_out, undriven_14, undriven_24);
  and and_16 (and_16_out, undriven_15, undriven_24);
  or or_1 (or_1_out, and_1_out, and_9_out);
  or or_2 (or_2_out, and_2_out, and_10_out);
  or or_3 (or_3_out, and_3_out, and_11_out);
  or or_4 (or_4_out, and_4_out, and_12_out);
  or or_5 (or_5_out, and_5_out, and_13_out);
  or or_6 (or_6_out, and_6_out, and_14_out);
  or or_7 (or_7_out, and_7_out, and_15_out);
  or or_8 (or_8_out, and_8_out, and_16_out);
  not not_2 (not_2_out, PC_LOAD);
  and and_17 (and_17_out, inc8_1_s0, not_2_out);
  and and_18 (and_18_out, inc8_1_s1, not_2_out);
  and and_19 (and_19_out, inc8_1_s2, not_2_out);
  and and_20 (and_20_out, inc8_1_s3, not_2_out);
  and and_21 (and_21_out, inc8_1_s4, not_2_out);
  and and_22 (and_22_out, inc8_1_s5, not_2_out);
  and and_23 (and_23_out, inc8_1_s6, not_2_out);
  and and_24 (and_24_out, inc8_1_s7, not_2_out);
  and and_25 (and_25_out, or_1_out, PC_LOAD);
  and and_26 (and_26_out, or_2_out, undriven_25);
  and and_27 (and_27_out, or_3_out, undriven_25);
  and and_28 (and_28_out, or_4_out, undriven_25);
  and and_29 (and_29_out, or_5_out, undriven_25);
  and and_30 (and_30_out, or_6_out, undriven_25);
  and and_31 (and_31_out, or_7_out, undriven_25);
  and and_32 (and_32_out, or_8_out, undriven_25);
  or or_9 (or_9_out[0], and_17_out, and_25_out);
  or or_10 (or_9_out[1], and_18_out, and_26_out);
  or or_11 (or_9_out[2], and_19_out, and_27_out);
  or or_12 (or_9_out[3], and_20_out, and_28_out);
  or or_13 (or_9_out[4], and_21_out, and_29_out);
  or or_14 (or_9_out[5], and_22_out, and_30_out);
  or or_15 (or_9_out[6], and_23_out, and_31_out);
  or or_16 (or_9_out[7], and_24_out, and_32_out);
  or or_17 (or_17_out, FETCH_WR, undriven_25);
endmodule

module PHASEGEN (
  input  CLK,
  output F,
  output FW,
  output E,
  output EW
);

  wire undriven;
  wire [1:0] not_1_out, register_1_q;

  Register #(.width(2), .trigger("rising")) register_1 (
    .D(not_1_out), .en(1'b1), .clk(CLK), .Q(register_1_q), .clr(1'b0));
  not not_1 (not_1_out[0], register_1_q[0]);
  xor xor_1 (not_1_out[1], register_1_q[1], register_1_q[0]);
  DECODER4B decoder4b_1 (
    .S0(register_1_q[0]), .S1(register_1_q[1]), .S2(1'b0), .S3(undriven), .D0(F), .D1(FW), .D2(E), .D3(EW));  // open: D4, D5, D6, D7, D8, D9, D10, D11, D12, D13, D14, D15
endmodule

module INC8 (
  input  A0,
  input  A1,
  input  A2,
  input  A3,
  input  A4,
  input  A5,
  input  A6,
  input  A7,
  output S0,
  output S1,
  output S2,
  output S3,
  output S4,
  output S5,
  output S6,
  output S7,
  output Cout
);

  wire and_1_out, and_2_out, and_3_out, and_4_out, and_5_out, and_6_out, and_7_out, undriven;

  xor xor_1 (S0, A0, 1'b1);
  and and_1 (and_1_out, A0, undriven);
  xor xor_2 (S1, A1, and_1_out);
  and and_2 (and_2_out, A1, and_1_out);
  xor xor_3 (S2, A2, and_2_out);
  and and_3 (and_3_out, A2, and_2_out);
  xor xor_4 (S3, A3, and_3_out);
  and and_4 (and_4_out, A3, and_3_out);
  xor xor_5 (S4, A4, and_4_out);
  and and_5 (and_5_out, A4, and_4_out);
  xor xor_6 (S5, A5, and_5_out);
  and and_6 (and_6_out, A5, and_5_out);
  xor xor_7 (S6, A6, and_6_out);
  and and_7 (and_7_out, A6, and_6_out);
  xor xor_8 (S7, A7, and_7_out);
  and and_8 (Cout, A7, and_7_out);
endmodule

module MUX2_16 (
  input  SEL,
  input  [15:0] A,
  input  [15:0] B,
  output [15:0] Y
);

  wire notb_1_y, undriven, undriven_2, undriven_3, undriven_4, undriven_5, undriven_6, undriven_7,
       undriven_8, undriven_9, undriven_10, undriven_11, undriven_12, undriven_13, undriven_14, undriven_15,
       undriven_16, undriven_17, undriven_18;

  NOTB notb_1 (.A(SEL), .Y(notb_1_y));
  BUSMUX2B busmux2b_1 (
    .a0(A[0]), .a1(A[1]), .a2(A[2]), .a3(A[3]), .b0(undriven_6), .b1(undriven_7), .b2(B[2]), .b3(undriven_8),
    .sA(notb_1_y), .sB(SEL), .y0(Y[0]), .y1(Y[1]), .y2(Y[2]), .y3(Y[3]));
  BUSMUX2B busmux2b_2 (
    .a0(A[4]), .a1(A[5]), .a2(A[6]), .a3(A[7]), .b0(undriven_9), .b1(undriven_10), .b2(undriven_11),
    .b3(undriven_12), .sA(undriven_5), .sB(SEL), .y0(Y[4]), .y1(Y[5]), .y2(Y[6]), .y3(Y[7]));
  BUSMUX2B busmux2b_3 (
    .a0(A[8]), .a1(A[9]), .a2(A[10]), .a3(A[11]), .b0(undriven_13), .b1(B[9]), .b2(undriven_14),
    .b3(undriven_15), .sA(notb_1_y), .sB(undriven), .y0(Y[8]), .y1(Y[9]), .y2(Y[10]), .y3(Y[11]));
  BUSMUX2B busmux2b_4 (
    .a0(undriven_2), .a1(undriven_3), .a2(undriven_4), .a3(A[15]), .b0(B[12]), .b1(B[13]), .b2(B[14]),
    .b3(undriven_16), .sA(undriven_17), .sB(undriven_18), .y0(Y[12]), .y1(Y[13]), .y2(Y[14]), .y3(Y[15]));
endmodule

module MUX2_8 (
  input  SEL,
  input  [7:0] A,
  input  [7:0] B,
  output [7:0] Y
);

  wire busmux2b_2_y0, busmux2b_2_y1, busmux2b_2_y2, busmux2b_2_y3, notb_1_y, undriven, undriven_2,
       undriven_3, undriven_4, undriven_5, undriven_6, undriven_7, undriven_8, undriven_9, undriven_10;

  NOTB notb_1 (.A(SEL), .Y(notb_1_y));
  BUSMUX2B busmux2b_1 (
    .a0(A[0]), .a1(A[1]), .a2(A[2]), .a3(A[3]), .b0(undriven_4), .b1(undriven_5), .b2(undriven_6), .b3(B[3]),
    .sA(notb_1_y), .sB(SEL), .y0(Y[0]), .y1(Y[1]), .y2(Y[2]), .y3(Y[3]));
  BUSMUX2B busmux2b_2 (
    .a0(A[4]), .a1(A[5]), .a2(undriven), .a3(undriven_2), .b0(undriven_7), .b1(undriven_8), .b2(undriven_9),
    .b3(undriven_10), .sA(undriven_3), .sB(SEL), .y0(busmux2b_2_y0), .y1(busmux2b_2_y1), .y2(busmux2b_2_y2),
    .y3(busmux2b_2_y3));
endmodule

module MUX2_4 (
  input  SEL,
  input  [3:0] A,
  input  [3:0] B,
  output [3:0] Y
);

  wire notb_1_y, undriven, undriven_2;

  NOTB notb_1 (.A(SEL), .Y(notb_1_y));
  BUSMUX2B busmux2b_1 (
    .a0(A[0]), .a1(A[1]), .a2(A[2]), .a3(A[3]), .b0(B[0]), .b1(B[1]), .b2(undriven), .b3(undriven_2),
    .sA(notb_1_y), .sB(SEL), .y0(Y[0]), .y1(Y[1]), .y2(Y[2]), .y3(Y[3]));
endmodule

module ADD16B (
  input  A0,
  input  B0,
  input  Cin,
  input  A1,
  input  B1,
  input  A2,
  input  B2,
  input  A3,
  input  B3,
  input  A4,
  input  B4,
  input  A5,
  input  B5,
  input  A6,
  input  B6,
  input  A7,
  input  B7,
  input  A8,
  input  B8,
  input  A9,
  input  B9,
  input  A10,
  input  B10,
  input  A11,
  input  B11,
  input  A12,
  input  B12,
  input  A13,
  input  B13,
  input  A14,
  input  B14,
  input  A15,
  input  B15,
  output S0,
  output Cout,
  output S1,
  output S2,
  output S3,
  output S4,
  output S5,
  output S6,
  output S7,
  output S8,
  output S9,
  output S10,
  output S11,
  output S12,
  output S13,
  output S14,
  output S15
);

  wire fulladdb_1_cout, fulladdb_2_cout, fulladdb_3_cout, fulladdb_4_cout, fulladdb_5_cout, fulladdb_6_cout,
       fulladdb_7_cout, fulladdb_8_cout, fulladdb_9_cout, fulladdb_10_cout, fulladdb_11_cout,
       fulladdb_12_cout, fulladdb_13_cout, fulladdb_14_cout, fulladdb_15_cout;

  FULLADDB fulladdb_1 (.A(A0), .B(B0), .Cin(Cin), .S(S0), .Cout(fulladdb_1_cout));
  FULLADDB fulladdb_2 (.A(A1), .B(B1), .Cin(fulladdb_1_cout), .S(S1), .Cout(fulladdb_2_cout));
  FULLADDB fulladdb_3 (.A(A2), .B(B2), .Cin(fulladdb_2_cout), .S(S2), .Cout(fulladdb_3_cout));
  FULLADDB fulladdb_4 (.A(A3), .B(B3), .Cin(fulladdb_3_cout), .S(S3), .Cout(fulladdb_4_cout));
  FULLADDB fulladdb_5 (.A(A4), .B(B4), .Cin(fulladdb_4_cout), .S(S4), .Cout(fulladdb_5_cout));
  FULLADDB fulladdb_6 (.A(A5), .B(B5), .Cin(fulladdb_5_cout), .S(S5), .Cout(fulladdb_6_cout));
  FULLADDB fulladdb_7 (.A(A6), .B(B6), .Cin(fulladdb_6_cout), .S(S6), .Cout(fulladdb_7_cout));
  FULLADDB fulladdb_8 (.A(A7), .B(B7), .Cin(fulladdb_7_cout), .S(S7), .Cout(fulladdb_8_cout));
  FULLADDB fulladdb_9 (.A(A8), .B(B8), .Cin(fulladdb_8_cout), .S(S8), .Cout(fulladdb_9_cout));
  FULLADDB fulladdb_10 (.A(A9), .B(B9), .Cin(fulladdb_9_cout), .S(S9), .Cout(fulladdb_10_cout));
  FULLADDB fulladdb_11 (.A(A10), .B(B10), .Cin(fulladdb_10_cout), .S(S10), .Cout(fulladdb_11_cout));
  FULLADDB fulladdb_12 (.A(A11), .B(B11), .Cin(fulladdb_11_cout), .S(S11), .Cout(fulladdb_12_cout));
  FULLADDB fulladdb_13 (.A(A12), .B(B12), .Cin(fulladdb_12_cout), .S(S12), .Cout(fulladdb_13_cout));
  FULLADDB fulladdb_14 (.A(A13), .B(B13), .Cin(fulladdb_13_cout), .S(S13), .Cout(fulladdb_14_cout));
  FULLADDB fulladdb_15 (.A(A14), .B(B14), .Cin(fulladdb_14_cout), .S(S14), .Cout(fulladdb_15_cout));
  FULLADDB fulladdb_16 (.A(A15), .B(B15), .Cin(fulladdb_15_cout), .S(S15), .Cout(Cout));
endmodule

module AND16B (
  input  A0,
  input  B0,
  input  A1,
  input  B1,
  input  A2,
  input  B2,
  input  A3,
  input  B3,
  input  A4,
  input  B4,
  input  A5,
  input  B5,
  input  A6,
  input  B6,
  input  A7,
  input  B7,
  input  A8,
  input  B8,
  input  A9,
  input  B9,
  input  A10,
  input  B10,
  input  A11,
  input  B11,
  input  A12,
  input  B12,
  input  A13,
  input  B13,
  input  A14,
  input  B14,
  input  A15,
  input  B15,
  output Y0,
  output Y1,
  output Y2,
  output Y3,
  output Y4,
  output Y5,
  output Y6,
  output Y7,
  output Y8,
  output Y9,
  output Y10,
  output Y11,
  output Y12,
  output Y13,
  output Y14,
  output Y15
);

  ANDB andb_1 (.A(A0), .B(B0), .Y(Y0));
  ANDB andb_2 (.A(A1), .B(B1), .Y(Y1));
  ANDB andb_3 (.A(A2), .B(B2), .Y(Y2));
  ANDB andb_4 (.A(A3), .B(B3), .Y(Y3));
  ANDB andb_5 (.A(A4), .B(B4), .Y(Y4));
  ANDB andb_6 (.A(A5), .B(B5), .Y(Y5));
  ANDB andb_7 (.A(A6), .B(B6), .Y(Y6));
  ANDB andb_8 (.A(A7), .B(B7), .Y(Y7));
  ANDB andb_9 (.A(A8), .B(B8), .Y(Y8));
  ANDB andb_10 (.A(A9), .B(B9), .Y(Y9));
  ANDB andb_11 (.A(A10), .B(B10), .Y(Y10));
  ANDB andb_12 (.A(A11), .B(B11), .Y(Y11));
  ANDB andb_13 (.A(A12), .B(B12), .Y(Y12));
  ANDB andb_14 (.A(A13), .B(B13), .Y(Y13));
  ANDB andb_15 (.A(A14), .B(B14), .Y(Y14));
  ANDB andb_16 (.A(A15), .B(B15), .Y(Y15));
endmodule

module XOR16B (
  input  A0,
  input  B0,
  input  A1,
  input  B1,
  input  A2,
  input  B2,
  input  A3,
  input  B3,
  input  A4,
  input  B4,
  input  A5,
  input  B5,
  input  A6,
  input  B6,
  input  A7,
  input  B7,
  input  A8,
  input  B8,
  input  A9,
  input  B9,
  input  A10,
  input  B10,
  input  A11,
  input  B11,
  input  A12,
  input  B12,
  input  A13,
  input  B13,
  input  A14,
  input  B14,
  input  A15,
  input  B15,
  output Y0,
  output Y1,
  output Y2,
  output Y3,
  output Y4,
  output Y5,
  output Y6,
  output Y7,
  output Y8,
  output Y9,
  output Y10,
  output Y11,
  output Y12,
  output Y13,
  output Y14,
  output Y15
);

  XORB xorb_1 (.A(A0), .B(B0), .Y(Y0));
  XORB xorb_2 (.A(A1), .B(B1), .Y(Y1));
  XORB xorb_3 (.A(A2), .B(B2), .Y(Y2));
  XORB xorb_4 (.A(A3), .B(B3), .Y(Y3));
  XORB xorb_5 (.A(A4), .B(B4), .Y(Y4));
  XORB xorb_6 (.A(A5), .B(B5), .Y(Y5));
  XORB xorb_7 (.A(A6), .B(B6), .Y(Y6));
  XORB xorb_8 (.A(A7), .B(B7), .Y(Y7));
  XORB xorb_9 (.A(A8), .B(B8), .Y(Y8));
  XORB xorb_10 (.A(A9), .B(B9), .Y(Y9));
  XORB xorb_11 (.A(A10), .B(B10), .Y(Y10));
  XORB xorb_12 (.A(A11), .B(B11), .Y(Y11));
  XORB xorb_13 (.A(A12), .B(B12), .Y(Y12));
  XORB xorb_14 (.A(A13), .B(B13), .Y(Y13));
  XORB xorb_15 (.A(A14), .B(B14), .Y(Y14));
  XORB xorb_16 (.A(A15), .B(B15), .Y(Y15));
endmodule

module OR16B (
  input  i0,
  input  i1,
  input  i2,
  input  i3,
  input  i4,
  input  i5,
  input  i6,
  input  i7,
  input  i8,
  input  i9,
  input  i10,
  input  i11,
  input  i12,
  input  i13,
  input  i14,
  input  i15,
  output Y
);

  wire or_1_out, or_2_out, or_3_out, or_4_out, or_5_out, or_6_out, or_7_out, or_8_out, or_9_out, or_10_out,
       or_11_out, or_12_out, or_13_out, or_14_out;

  or or_1 (or_1_out, i0, i1);
  or or_2 (or_2_out, or_1_out, i2);
  or or_3 (or_3_out, or_2_out, i3);
  or or_4 (or_4_out, or_3_out, i4);
  or or_5 (or_5_out, or_4_out, i5);
  or or_6 (or_6_out, or_5_out, i6);
  or or_7 (or_7_out, or_6_out, i7);
  or or_8 (or_8_out, or_7_out, i8);
  or or_9 (or_9_out, or_8_out, i9);
  or or_10 (or_10_out, or_9_out, i10);
  or or_11 (or_11_out, or_10_out, i11);
  or or_12 (or_12_out, or_11_out, i12);
  or or_13 (or_13_out, or_12_out, i13);
  or or_14 (or_14_out, or_13_out, i14);
  or or_15 (Y, or_14_out, i15);
endmodule

module LSHIFT16B (
  input  A0,
  input  N0,
  input  A1,
  input  N1,
  input  A2,
  input  N2,
  input  A3,
  input  N3,
  input  A4,
  input  A5,
  input  A6,
  input  A7,
  input  A8,
  input  A9,
  input  A10,
  input  A11,
  input  A12,
  input  A13,
  input  A14,
  input  A15,
  output Y0,
  output Y1,
  output Y2,
  output Y3,
  output Y4,
  output Y5,
  output Y6,
  output Y7,
  output Y8,
  output Y9,
  output Y10,
  output Y11,
  output Y12,
  output Y13,
  output Y14,
  output Y15
);

  wire busmux2b_1_y0, busmux2b_1_y1, busmux2b_1_y2, busmux2b_1_y3, busmux2b_2_y0, busmux2b_2_y1,
       busmux2b_2_y2, busmux2b_2_y3, busmux2b_3_y0, busmux2b_3_y1, busmux2b_3_y2, busmux2b_3_y3,
       busmux2b_4_y0, busmux2b_4_y1, busmux2b_4_y2, busmux2b_4_y3, busmux2b_5_y0, busmux2b_5_y1,
       busmux2b_5_y2, busmux2b_5_y3, busmux2b_6_y0, busmux2b_6_y1, busmux2b_6_y2, busmux2b_6_y3,
       busmux2b_7_y0, busmux2b_7_y1, busmux2b_7_y2, busmux2b_7_y3, busmux2b_8_y0, busmux2b_8_y1,
       busmux2b_8_y2, busmux2b_8_y3, busmux2b_9_y0, busmux2b_9_y1, busmux2b_9_y2, busmux2b_9_y3,
       busmux2b_10_y0, busmux2b_10_y1, busmux2b_10_y2, busmux2b_10_y3, busmux2b_11_y0, busmux2b_11_y1,
       busmux2b_11_y2, busmux2b_11_y3, busmux2b_12_y0, busmux2b_12_y1, busmux2b_12_y2, busmux2b_12_y3,
       notb_1_y, notb_2_y, notb_3_y, notb_4_y, undriven, undriven_2, undriven_3, undriven_4, undriven_5,
       undriven_6, undriven_7, undriven_8, undriven_9, undriven_10, undriven_11, undriven_12, undriven_13,
       undriven_14, undriven_15, undriven_16, undriven_17, undriven_18, undriven_19, undriven_20,
       undriven_21, undriven_22, undriven_23, undriven_24, undriven_25, undriven_26;

  NOTB notb_1 (.A(N0), .Y(notb_1_y));
  BUSMUX2B busmux2b_1 (
    .a0(A0), .a1(A1), .a2(A2), .a3(A3), .b0(1'b0), .b1(undriven_2), .b2(A1), .b3(undriven), .sA(notb_1_y),
    .sB(N0), .y0(busmux2b_1_y0), .y1(busmux2b_1_y1), .y2(busmux2b_1_y2), .y3(busmux2b_1_y3));
  BUSMUX2B busmux2b_2 (
    .a0(A4), .a1(A5), .a2(A6), .a3(A7), .b0(A3), .b1(undriven_7), .b2(undriven_6), .b3(A6), .sA(undriven_3),
    .sB(undriven_5), .y0(busmux2b_2_y0), .y1(busmux2b_2_y1), .y2(busmux2b_2_y2), .y3(busmux2b_2_y3));
  BUSMUX2B busmux2b_3 (
    .a0(A8), .a1(A9), .a2(A10), .a3(A11), .b0(A7), .b1(A8), .b2(A9), .b3(A10), .sA(undriven_3),
    .sB(undriven_5), .y0(busmux2b_3_y0), .y1(busmux2b_3_y1), .y2(busmux2b_3_y2), .y3(busmux2b_3_y3));
  BUSMUX2B busmux2b_4 (
    .a0(A12), .a1(A13), .a2(A14), .a3(A15), .b0(A11), .b1(undriven_10), .b2(undriven_9), .b3(undriven_8),
    .sA(undriven_3), .sB(undriven_5), .y0(busmux2b_4_y0), .y1(busmux2b_4_y1), .y2(busmux2b_4_y2),
    .y3(busmux2b_4_y3));
  NOTB notb_2 (.A(N1), .Y(notb_2_y));
  BUSMUX2B busmux2b_5 (
    .a0(busmux2b_1_y0), .a1(busmux2b_1_y1), .a2(busmux2b_1_y2), .a3(busmux2b_1_y3), .b0(undriven_4),
    .b1(undriven_12), .b2(busmux2b_1_y0), .b3(busmux2b_1_y1), .sA(notb_2_y), .sB(N1), .y0(busmux2b_5_y0),
    .y1(busmux2b_5_y1), .y2(busmux2b_5_y2), .y3(busmux2b_5_y3));
  BUSMUX2B busmux2b_6 (
    .a0(busmux2b_2_y0), .a1(busmux2b_2_y1), .a2(busmux2b_2_y2), .a3(busmux2b_2_y3), .b0(busmux2b_1_y2),
    .b1(busmux2b_1_y3), .b2(busmux2b_2_y0), .b3(busmux2b_2_y1), .sA(undriven_11), .sB(undriven_13),
    .y0(busmux2b_6_y0), .y1(busmux2b_6_y1), .y2(busmux2b_6_y2), .y3(busmux2b_6_y3));
  BUSMUX2B busmux2b_7 (
    .a0(busmux2b_3_y0), .a1(busmux2b_3_y1), .a2(busmux2b_3_y2), .a3(busmux2b_3_y3), .b0(busmux2b_2_y2),
    .b1(busmux2b_2_y3), .b2(busmux2b_3_y0), .b3(busmux2b_3_y1), .sA(undriven_11), .sB(undriven_13),
    .y0(busmux2b_7_y0), .y1(busmux2b_7_y1), .y2(busmux2b_7_y2), .y3(busmux2b_7_y3));
  BUSMUX2B busmux2b_8 (
    .a0(busmux2b_4_y0), .a1(busmux2b_4_y1), .a2(busmux2b_4_y2), .a3(busmux2b_4_y3), .b0(busmux2b_3_y2),
    .b1(busmux2b_3_y3), .b2(busmux2b_4_y0), .b3(busmux2b_4_y1), .sA(undriven_11), .sB(undriven_13),
    .y0(busmux2b_8_y0), .y1(busmux2b_8_y1), .y2(busmux2b_8_y2), .y3(busmux2b_8_y3));
  NOTB notb_3 (.A(N2), .Y(notb_3_y));
  BUSMUX2B busmux2b_9 (
    .a0(busmux2b_5_y0), .a1(busmux2b_5_y1), .a2(busmux2b_5_y2), .a3(busmux2b_5_y3), .b0(undriven_4),
    .b1(undriven_4), .b2(undriven_4), .b3(undriven_4), .sA(notb_3_y), .sB(N2), .y0(busmux2b_9_y0),
    .y1(busmux2b_9_y1), .y2(busmux2b_9_y2), .y3(busmux2b_9_y3));
  BUSMUX2B busmux2b_10 (
    .a0(busmux2b_6_y0), .a1(busmux2b_6_y1), .a2(busmux2b_6_y2), .a3(busmux2b_6_y3), .b0(busmux2b_5_y0),
    .b1(busmux2b_5_y1), .b2(busmux2b_5_y2), .b3(undriven_14), .sA(undriven_15), .sB(undriven_17),
    .y0(busmux2b_10_y0), .y1(busmux2b_10_y1), .y2(busmux2b_10_y2), .y3(busmux2b_10_y3));
  BUSMUX2B busmux2b_11 (
    .a0(busmux2b_7_y0), .a1(busmux2b_7_y1), .a2(busmux2b_7_y2), .a3(busmux2b_7_y3), .b0(undriven_19),
    .b1(undriven_18), .b2(undriven_20), .b3(busmux2b_6_y3), .sA(undriven_15), .sB(undriven_17),
    .y0(busmux2b_11_y0), .y1(busmux2b_11_y1), .y2(busmux2b_11_y2), .y3(busmux2b_11_y3));
  BUSMUX2B busmux2b_12 (
    .a0(busmux2b_8_y0), .a1(busmux2b_8_y1), .a2(busmux2b_8_y2), .a3(busmux2b_8_y3), .b0(busmux2b_7_y0),
    .b1(busmux2b_7_y1), .b2(busmux2b_7_y2), .b3(undriven_21), .sA(undriven_15), .sB(undriven_17),
    .y0(busmux2b_12_y0), .y1(busmux2b_12_y1), .y2(busmux2b_12_y2), .y3(busmux2b_12_y3));
  NOTB notb_4 (.A(N3), .Y(notb_4_y));
  BUSMUX2B busmux2b_13 (
    .a0(busmux2b_9_y0), .a1(busmux2b_9_y1), .a2(busmux2b_9_y2), .a3(busmux2b_9_y3), .b0(undriven_16),
    .b1(undriven_16), .b2(undriven_16), .b3(undriven_16), .sA(notb_4_y), .sB(N3), .y0(Y0), .y1(Y1), .y2(Y2),
    .y3(Y3));
  BUSMUX2B busmux2b_14 (
    .a0(busmux2b_10_y0), .a1(busmux2b_10_y1), .a2(busmux2b_10_y2), .a3(busmux2b_10_y3), .b0(undriven_16),
    .b1(undriven_16), .b2(undriven_16), .b3(undriven_16), .sA(undriven_22), .sB(undriven_23), .y0(Y4),
    .y1(Y5), .y2(Y6), .y3(Y7));
  BUSMUX2B busmux2b_15 (
    .a0(busmux2b_11_y0), .a1(busmux2b_11_y1), .a2(busmux2b_11_y2), .a3(busmux2b_11_y3), .b0(busmux2b_9_y0),
    .b1(busmux2b_9_y1), .b2(busmux2b_9_y2), .b3(busmux2b_9_y3), .sA(undriven_22), .sB(undriven_23), .y0(Y8),
    .y1(Y9), .y2(Y10), .y3(Y11));
  BUSMUX2B busmux2b_16 (
    .a0(busmux2b_12_y0), .a1(busmux2b_12_y1), .a2(busmux2b_12_y2), .a3(busmux2b_12_y3), .b0(busmux2b_10_y0),
    .b1(undriven_25), .b2(undriven_26), .b3(undriven_24), .sA(undriven_22), .sB(undriven_23), .y0(Y12),
    .y1(Y13), .y2(Y14), .y3(Y15));
endmodule

module RSHIFT16B (
  input  A0,
  input  N0,
  input  A1,
  input  N1,
  input  A2,
  input  N2,
  input  A3,
  input  N3,
  input  A4,
  input  A5,
  input  A6,
  input  A7,
  input  A8,
  input  A9,
  input  A10,
  input  A11,
  input  A12,
  input  A13,
  input  A14,
  input  A15,
  output Y0,
  output Y1,
  output Y2,
  output Y3,
  output Y4,
  output Y5,
  output Y6,
  output Y7,
  output Y8,
  output Y9,
  output Y10,
  output Y11,
  output Y12,
  output Y13,
  output Y14,
  output Y15
);

  wire busmux2b_1_y0, busmux2b_1_y1, busmux2b_1_y2, busmux2b_1_y3, busmux2b_2_y0, busmux2b_2_y1,
       busmux2b_2_y2, busmux2b_2_y3, busmux2b_3_y0, busmux2b_3_y1, busmux2b_3_y2, busmux2b_3_y3,
       busmux2b_4_y0, busmux2b_4_y1, busmux2b_4_y2, busmux2b_4_y3, busmux2b_5_y0, busmux2b_5_y1,
       busmux2b_5_y2, busmux2b_5_y3, busmux2b_6_y0, busmux2b_6_y1, busmux2b_6_y2, busmux2b_6_y3,
       busmux2b_7_y0, busmux2b_7_y1, busmux2b_7_y2, busmux2b_7_y3, busmux2b_8_y0, busmux2b_8_y1,
       busmux2b_8_y2, busmux2b_8_y3, busmux2b_9_y0, busmux2b_9_y1, busmux2b_9_y2, busmux2b_9_y3,
       busmux2b_10_y0, busmux2b_10_y1, busmux2b_10_y2, busmux2b_10_y3, busmux2b_11_y0, busmux2b_11_y1,
       busmux2b_11_y2, busmux2b_11_y3, busmux2b_12_y0, busmux2b_12_y1, busmux2b_12_y2, busmux2b_12_y3,
       notb_1_y, notb_2_y, notb_3_y, notb_4_y, undriven, undriven_2, undriven_3, undriven_4, undriven_5,
       undriven_6, undriven_7, undriven_8, undriven_9, undriven_10, undriven_11, undriven_12, undriven_13,
       undriven_14, undriven_15, undriven_16, undriven_17, undriven_18, undriven_19, undriven_20,
       undriven_21, undriven_22, undriven_23, undriven_24, undriven_25, undriven_26, undriven_27,
       undriven_28, undriven_29, undriven_30, undriven_31, undriven_32, undriven_33, undriven_34,
       undriven_35, undriven_36, undriven_37, undriven_38, undriven_39, undriven_40, undriven_41,
       undriven_42, undriven_43, undriven_44, undriven_45, undriven_46, undriven_47, undriven_48,
       undriven_49, undriven_50, undriven_51;

  NOTB notb_1 (.A(N0), .Y(notb_1_y));
  BUSMUX2B busmux2b_1 (
    .a0(A0), .a1(A1), .a2(A2), .a3(A3), .b0(A1), .b1(undriven), .b2(A3), .b3(A4), .sA(notb_1_y), .sB(N0),
    .y0(busmux2b_1_y0), .y1(busmux2b_1_y1), .y2(busmux2b_1_y2), .y3(busmux2b_1_y3));
  BUSMUX2B busmux2b_2 (
    .a0(A4), .a1(A5), .a2(A6), .a3(A7), .b0(undriven_5), .b1(undriven_4), .b2(undriven_3), .b3(A8),
    .sA(notb_1_y), .sB(undriven_2), .y0(busmux2b_2_y0), .y1(busmux2b_2_y1), .y2(busmux2b_2_y2),
    .y3(busmux2b_2_y3));
  BUSMUX2B busmux2b_3 (
    .a0(A8), .a1(A9), .a2(A10), .a3(A11), .b0(undriven_8), .b1(undriven_7), .b2(undriven_6), .b3(A12),
    .sA(notb_1_y), .sB(undriven_2), .y0(busmux2b_3_y0), .y1(busmux2b_3_y1), .y2(busmux2b_3_y2),
    .y3(busmux2b_3_y3));
  BUSMUX2B busmux2b_4 (
    .a0(A12), .a1(A13), .a2(A14), .a3(A15), .b0(undriven_11), .b1(undriven_10), .b2(undriven_9), .b3(1'b0),
    .sA(notb_1_y), .sB(undriven_2), .y0(busmux2b_4_y0), .y1(busmux2b_4_y1), .y2(busmux2b_4_y2),
    .y3(busmux2b_4_y3));
  NOTB notb_2 (.A(N1), .Y(notb_2_y));
  BUSMUX2B busmux2b_5 (
    .a0(busmux2b_1_y0), .a1(busmux2b_1_y1), .a2(busmux2b_1_y2), .a3(busmux2b_1_y3), .b0(undriven_14),
    .b1(undriven_12), .b2(busmux2b_2_y0), .b3(busmux2b_2_y1), .sA(notb_2_y), .sB(N1), .y0(busmux2b_5_y0),
    .y1(busmux2b_5_y1), .y2(busmux2b_5_y2), .y3(busmux2b_5_y3));
  BUSMUX2B busmux2b_6 (
    .a0(undriven_15), .a1(busmux2b_2_y1), .a2(busmux2b_2_y2), .a3(busmux2b_2_y3), .b0(undriven_17),
    .b1(busmux2b_2_y3), .b2(busmux2b_3_y0), .b3(busmux2b_3_y1), .sA(undriven_13), .sB(undriven_16),
    .y0(busmux2b_6_y0), .y1(busmux2b_6_y1), .y2(busmux2b_6_y2), .y3(busmux2b_6_y3));
  BUSMUX2B busmux2b_7 (
    .a0(undriven_18), .a1(busmux2b_3_y1), .a2(busmux2b_3_y2), .a3(busmux2b_3_y3), .b0(undriven_20),
    .b1(undriven_19), .b2(busmux2b_4_y0), .b3(busmux2b_4_y1), .sA(undriven_13), .sB(undriven_16),
    .y0(busmux2b_7_y0), .y1(busmux2b_7_y1), .y2(busmux2b_7_y2), .y3(busmux2b_7_y3));
  BUSMUX2B busmux2b_8 (
    .a0(undriven_21), .a1(busmux2b_4_y1), .a2(busmux2b_4_y2), .a3(busmux2b_4_y3), .b0(undriven_23),
    .b1(undriven_22), .b2(1'b0), .b3(undriven_24), .sA(undriven_13), .sB(undriven_16), .y0(busmux2b_8_y0),
    .y1(busmux2b_8_y1), .y2(busmux2b_8_y2), .y3(busmux2b_8_y3));
  NOTB notb_3 (.A(N2), .Y(notb_3_y));
  BUSMUX2B busmux2b_9 (
    .a0(busmux2b_5_y0), .a1(busmux2b_5_y1), .a2(busmux2b_5_y2), .a3(busmux2b_5_y3), .b0(busmux2b_6_y0),
    .b1(busmux2b_6_y1), .b2(busmux2b_6_y2), .b3(busmux2b_6_y3), .sA(notb_3_y), .sB(N2), .y0(busmux2b_9_y0),
    .y1(busmux2b_9_y1), .y2(busmux2b_9_y2), .y3(busmux2b_9_y3));
  BUSMUX2B busmux2b_10 (
    .a0(busmux2b_6_y0), .a1(undriven_28), .a2(undriven_26), .a3(undriven_25), .b0(busmux2b_7_y0),
    .b1(busmux2b_7_y1), .b2(busmux2b_7_y2), .b3(busmux2b_7_y3), .sA(undriven_27), .sB(undriven_29),
    .y0(busmux2b_10_y0), .y1(busmux2b_10_y1), .y2(busmux2b_10_y2), .y3(busmux2b_10_y3));
  BUSMUX2B busmux2b_11 (
    .a0(undriven_30), .a1(busmux2b_7_y1), .a2(undriven_32), .a3(undriven_31), .b0(busmux2b_8_y0),
    .b1(busmux2b_8_y1), .b2(busmux2b_8_y2), .b3(busmux2b_8_y3), .sA(undriven_27), .sB(undriven_29),
    .y0(busmux2b_11_y0), .y1(busmux2b_11_y1), .y2(busmux2b_11_y2), .y3(busmux2b_11_y3));
  BUSMUX2B busmux2b_12 (
    .a0(undriven_34), .a1(undriven_35), .a2(busmux2b_8_y2), .a3(undriven_33), .b0(1'b0), .b1(undriven_36),
    .b2(undriven_37), .b3(undriven_38), .sA(undriven_27), .sB(undriven_29), .y0(busmux2b_12_y0),
    .y1(busmux2b_12_y1), .y2(busmux2b_12_y2), .y3(busmux2b_12_y3));
  NOTB notb_4 (.A(N3), .Y(notb_4_y));
  BUSMUX2B busmux2b_13 (
    .a0(busmux2b_9_y0), .a1(busmux2b_9_y1), .a2(busmux2b_9_y2), .a3(busmux2b_9_y3), .b0(busmux2b_11_y0),
    .b1(busmux2b_11_y1), .b2(busmux2b_11_y2), .b3(busmux2b_11_y3), .sA(notb_4_y), .sB(N3), .y0(Y0), .y1(Y1),
    .y2(Y2), .y3(Y3));
  BUSMUX2B busmux2b_14 (
    .a0(busmux2b_10_y0), .a1(busmux2b_10_y1), .a2(busmux2b_10_y2), .a3(busmux2b_10_y3), .b0(busmux2b_12_y0),
    .b1(busmux2b_12_y1), .b2(busmux2b_12_y2), .b3(busmux2b_12_y3), .sA(undriven_42), .sB(undriven_43),
    .y0(Y4), .y1(Y5), .y2(Y6), .y3(Y7));
  BUSMUX2B busmux2b_15 (
    .a0(undriven_40), .a1(undriven_39), .a2(undriven_41), .a3(busmux2b_11_y3), .b0(1'b0), .b1(undriven_46),
    .b2(undriven_47), .b3(undriven_48), .sA(undriven_42), .sB(undriven_43), .y0(Y8), .y1(Y9), .y2(Y10),
    .y3(Y11));
  BUSMUX2B busmux2b_16 (
    .a0(busmux2b_12_y0), .a1(undriven_45), .a2(busmux2b_12_y2), .a3(undriven_44), .b0(1'b0),
    .b1(undriven_49), .b2(undriven_50), .b3(undriven_51), .sA(undriven_42), .sB(undriven_43), .y0(Y12),
    .y1(Y13), .y2(Y14), .y3(Y15));
endmodule

module BUSMUX2B (
  input  a0,
  input  b0,
  input  sA,
  input  a1,
  input  b1,
  input  a2,
  input  b2,
  input  sB,
  input  a3,
  input  b3,
  output y0,
  output y1,
  output y2,
  output y3
);

  wire and_1_out, and_2_out, and_3_out, and_4_out, and_5_out, and_6_out, and_7_out, and_8_out, undriven;

  and and_1 (and_1_out, a0, sA);
  and and_2 (and_2_out, a1, sA);
  and and_3 (and_3_out, a2, sA);
  and and_4 (and_4_out, a3, sA);
  and and_5 (and_5_out, b0, sB);
  and and_6 (and_6_out, b1, undriven);
  and and_7 (and_7_out, b2, undriven);
  and and_8 (and_8_out, b3, undriven);
  or or_1 (y0, and_1_out, and_5_out);
  or or_2 (y1, and_2_out, and_6_out);
  or or_3 (y2, and_3_out, and_7_out);
  or or_4 (y3, and_4_out, and_8_out);
endmodule

module DECODER4B (
  input  S0,
  input  S1,
  input  S2,
  input  S3,
  output D0,
  output D1,
  output D2,
  output D3,
  output D4,
  output D5,
  output D6,
  output D7,
  output D8,
  output D9,
  output D10,
  output D11,
  output D12,
  output D13,
  output D14,
  output D15
);

  wire and_1_out, and_2_out, and_3_out, and_4_out, and_5_out, and_6_out, and_7_out, and_8_out, and_9_out,
       and_10_out, and_11_out, and_12_out, and_13_out, and_14_out, and_15_out, and_16_out, and_17_out,
       and_18_out, and_19_out, and_20_out, and_21_out, and_22_out, and_23_out, and_24_out, and_25_out,
       and_26_out, and_27_out, and_28_out, and_29_out, and_30_out, and_31_out, and_32_out, not_1_out,
       not_2_out, not_3_out, not_4_out, undriven, undriven_2, undriven_3, undriven_4, undriven_5;

  not not_1 (not_1_out, S0);
  not not_2 (not_2_out, S1);
  not not_3 (not_3_out, S2);
  not not_4 (not_4_out, S3);
  and and_1 (and_1_out, not_1_out, not_2_out);
  and and_2 (and_2_out, S0, not_2_out);
  and and_3 (and_3_out, not_1_out, S1);
  and and_4 (and_4_out, undriven_3, undriven_2);
  and and_5 (and_5_out, not_1_out, not_2_out);
  and and_6 (and_6_out, undriven_3, not_2_out);
  and and_7 (and_7_out, not_1_out, undriven_2);
  and and_8 (and_8_out, undriven_3, undriven_2);
  and and_9 (and_9_out, not_1_out, not_2_out);
  and and_10 (and_10_out, undriven_3, not_2_out);
  and and_11 (and_11_out, not_1_out, undriven_2);
  and and_12 (and_12_out, undriven_3, undriven_2);
  and and_13 (and_13_out, not_1_out, not_2_out);
  and and_14 (and_14_out, undriven_3, not_2_out);
  and and_15 (and_15_out, not_1_out, undriven_2);
  and and_16 (and_16_out, undriven_3, undriven_2);
  and and_17 (and_17_out, not_3_out, not_4_out);
  and and_18 (and_18_out, not_3_out, not_4_out);
  and and_19 (and_19_out, not_3_out, not_4_out);
  and and_20 (and_20_out, not_3_out, not_4_out);
  and and_21 (and_21_out, S2, not_4_out);
  and and_22 (and_22_out, undriven_5, not_4_out);
  and and_23 (and_23_out, undriven_5, not_4_out);
  and and_24 (and_24_out, undriven_5, not_4_out);
  and and_25 (and_25_out, not_3_out, undriven);
  and and_26 (and_26_out, not_3_out, undriven_4);
  and and_27 (and_27_out, not_3_out, undriven_4);
  and and_28 (and_28_out, not_3_out, undriven_4);
  and and_29 (and_29_out, undriven_5, undriven_4);
  and and_30 (and_30_out, undriven_5, undriven_4);
  and and_31 (and_31_out, undriven_5, undriven_4);
  and and_32 (and_32_out, undriven_5, undriven_4);
  and and_33 (D0, and_1_out, and_17_out);
  and and_34 (D1, and_2_out, and_18_out);
  and and_35 (D2, and_3_out, and_19_out);
  and and_36 (D3, and_4_out, and_20_out);
  and and_37 (D4, and_5_out, and_21_out);
  and and_38 (D5, and_6_out, and_22_out);
  and and_39 (D6, and_7_out, and_23_out);
  and and_40 (D7, and_8_out, and_24_out);
  and and_41 (D8, and_9_out, and_25_out);
  and and_42 (D9, and_10_out, and_26_out);
  and and_43 (D10, and_11_out, and_27_out);
  and and_44 (D11, and_12_out, and_28_out);
  and and_45 (D12, and_13_out, and_29_out);
  and and_46 (D13, and_14_out, and_30_out);
  and and_47 (D14, and_15_out, and_31_out);
  and and_48 (D15, and_16_out, and_32_out);
endmodule

module FULLADDB (
  input  A,
  input  B,
  input  Cin,
  output S,
  output Cout
);

  wire and_1_out, and_2_out, undriven, undriven_2, undriven_3, xor_1_out;

  xor xor_1 (xor_1_out, A, B);
  and and_1 (and_1_out, undriven_2, undriven);
  xor xor_2 (S, xor_1_out, Cin);
  and and_2 (and_2_out, xor_1_out, undriven_3);
  or or_1 (Cout, and_1_out, and_2_out);
endmodule

module ANDB (
  input  A,
  input  B,
  output Y
);

  and and_1 (Y, A, B);
endmodule

module NOTB (
  input  A,
  output Y
);

  not not_1 (Y, A);
endmodule

module XORB (
  input  A,
  input  B,
  output Y
);

  xor xor_1 (Y, A, B);
endmodule

module ADD16 (
  input  A0,
  input  B0,
  input  Cin,
  input  A1,
  input  B1,
  input  A2,
  input  B2,
  input  A3,
  input  B3,
  input  A4,
  input  B4,
  input  A5,
  input  B5,
  input  A6,
  input  B6,
  input  A7,
  input  B7,
  input  A8,
  input  B8,
  input  A9,
  input  B9,
  input  A10,
  input  B10,
  input  A11,
  input  B11,
  input  A12,
  input  B12,
  input  A13,
  input  B13,
  input  A14,
  input  B14,
  input  A15,
  input  B15,
  output S0,
  output Cout,
  output S1,
  output S2,
  output S3,
  output S4,
  output S5,
  output S6,
  output S7,
  output S8,
  output S9,
  output S10,
  output S11,
  output S12,
  output S13,
  output S14,
  output S15
);

  wire add8_1_cout;

  ADD8 add8_1 (
    .A0(A0), .A1(A1), .A2(A2), .A3(A3), .A4(A4), .A5(A5), .A6(A6), .A7(A7), .B0(B0), .B1(B1), .B2(B2),
    .B3(B3), .B4(B4), .B5(B5), .B6(B6), .B7(B7), .Cin(Cin), .S0(S0), .S1(S1), .S2(S2), .S3(S3), .S4(S4),
    .S5(S5), .S6(S6), .S7(S7), .Cout(add8_1_cout));
  ADD8 add8_2 (
    .A0(A8), .A1(A9), .A2(A10), .A3(A11), .A4(A12), .A5(A13), .A6(A14), .A7(A15), .B0(B8), .B1(B9), .B2(B10),
    .B3(B11), .B4(B12), .B5(B13), .B6(B14), .B7(B15), .Cin(add8_1_cout), .S0(S8), .S1(S9), .S2(S10),
    .S3(S11), .S4(S12), .S5(S13), .S6(S14), .S7(S15), .Cout(Cout));
endmodule

module AND16 (
  input  A0,
  input  B0,
  input  A1,
  input  B1,
  input  A2,
  input  B2,
  input  A3,
  input  B3,
  input  A4,
  input  B4,
  input  A5,
  input  B5,
  input  A6,
  input  B6,
  input  A7,
  input  B7,
  input  A8,
  input  B8,
  input  A9,
  input  B9,
  input  A10,
  input  B10,
  input  A11,
  input  B11,
  input  A12,
  input  B12,
  input  A13,
  input  B13,
  input  A14,
  input  B14,
  input  A15,
  input  B15,
  output Y0,
  output Y1,
  output Y2,
  output Y3,
  output Y4,
  output Y5,
  output Y6,
  output Y7,
  output Y8,
  output Y9,
  output Y10,
  output Y11,
  output Y12,
  output Y13,
  output Y14,
  output Y15
);

  AND8 and8_1 (
    .A0(A0), .A1(A1), .A2(A2), .A3(A3), .A4(A4), .A5(A5), .A6(A6), .A7(A7), .B0(B0), .B1(B1), .B2(B2),
    .B3(B3), .B4(B4), .B5(B5), .B6(B6), .B7(B7), .Y0(Y0), .Y1(Y1), .Y2(Y2), .Y3(Y3), .Y4(Y4), .Y5(Y5),
    .Y6(Y6), .Y7(Y7));
  AND8 and8_2 (
    .A0(A8), .A1(A9), .A2(A10), .A3(A11), .A4(A12), .A5(A13), .A6(A14), .A7(A15), .B0(B8), .B1(B9), .B2(B10),
    .B3(B11), .B4(B12), .B5(B13), .B6(B14), .B7(B15), .Y0(Y8), .Y1(Y9), .Y2(Y10), .Y3(Y11), .Y4(Y12),
    .Y5(Y13), .Y6(Y14), .Y7(Y15));
endmodule

module XOR16 (
  input  A0,
  input  B0,
  input  A1,
  input  B1,
  input  A2,
  input  B2,
  input  A3,
  input  B3,
  input  A4,
  input  B4,
  input  A5,
  input  B5,
  input  A6,
  input  B6,
  input  A7,
  input  B7,
  input  A8,
  input  B8,
  input  A9,
  input  B9,
  input  A10,
  input  B10,
  input  A11,
  input  B11,
  input  A12,
  input  B12,
  input  A13,
  input  B13,
  input  A14,
  input  B14,
  input  A15,
  input  B15,
  output Y0,
  output Y1,
  output Y2,
  output Y3,
  output Y4,
  output Y5,
  output Y6,
  output Y7,
  output Y8,
  output Y9,
  output Y10,
  output Y11,
  output Y12,
  output Y13,
  output Y14,
  output Y15
);

  XOR8 xor8_1 (
    .A0(A0), .A1(A1), .A2(A2), .A3(A3), .A4(A4), .A5(A5), .A6(A6), .A7(A7), .B0(B0), .B1(B1), .B2(B2),
    .B3(B3), .B4(B4), .B5(B5), .B6(B6), .B7(B7), .Y0(Y0), .Y1(Y1), .Y2(Y2), .Y3(Y3), .Y4(Y4), .Y5(Y5),
    .Y6(Y6), .Y7(Y7));
  XOR8 xor8_2 (
    .A0(A8), .A1(A9), .A2(A10), .A3(A11), .A4(A12), .A5(A13), .A6(A14), .A7(A15), .B0(B8), .B1(B9), .B2(B10),
    .B3(B11), .B4(B12), .B5(B13), .B6(B14), .B7(B15), .Y0(Y8), .Y1(Y9), .Y2(Y10), .Y3(Y11), .Y4(Y12),
    .Y5(Y13), .Y6(Y14), .Y7(Y15));
endmodule

module OR16 (
  input  i0,
  input  i1,
  input  i2,
  input  i3,
  input  i4,
  input  i5,
  input  i6,
  input  i7,
  input  i8,
  input  i9,
  input  i10,
  input  i11,
  input  i12,
  input  i13,
  input  i14,
  input  i15,
  output Y
);

  wire or_1_y, or_2_y, or_3_y, or_4_y, or_5_y, or_6_y, or_7_y, or_8_y, or_9_y, or_10_y, or_11_y, or_12_y,
       or_13_y, or_14_y;

  OR or_1 (.A(i0), .B(i1), .Y(or_1_y));
  OR or_2 (.A(or_1_y), .B(i2), .Y(or_2_y));
  OR or_3 (.A(or_2_y), .B(i3), .Y(or_3_y));
  OR or_4 (.A(or_3_y), .B(i4), .Y(or_4_y));
  OR or_5 (.A(or_4_y), .B(i5), .Y(or_5_y));
  OR or_6 (.A(or_5_y), .B(i6), .Y(or_6_y));
  OR or_7 (.A(or_6_y), .B(i7), .Y(or_7_y));
  OR or_8 (.A(or_7_y), .B(i8), .Y(or_8_y));
  OR or_9 (.A(or_8_y), .B(i9), .Y(or_9_y));
  OR or_10 (.A(or_9_y), .B(i10), .Y(or_10_y));
  OR or_11 (.A(or_10_y), .B(i11), .Y(or_11_y));
  OR or_12 (.A(or_11_y), .B(i12), .Y(or_12_y));
  OR or_13 (.A(or_12_y), .B(i13), .Y(or_13_y));
  OR or_14 (.A(or_13_y), .B(i14), .Y(or_14_y));
  OR or_15 (.A(or_14_y), .B(i15), .Y(Y));
endmodule

module LSHIFT16 (
  input  A0,
  input  N0,
  input  A1,
  input  N1,
  input  A2,
  input  N2,
  input  A3,
  input  N3,
  input  A4,
  input  A5,
  input  A6,
  input  A7,
  input  A8,
  input  A9,
  input  A10,
  input  A11,
  input  A12,
  input  A13,
  input  A14,
  input  A15,
  output Y0,
  output Y1,
  output Y2,
  output Y3,
  output Y4,
  output Y5,
  output Y6,
  output Y7,
  output Y8,
  output Y9,
  output Y10,
  output Y11,
  output Y12,
  output Y13,
  output Y14,
  output Y15
);

  wire busmux2_1_y0, busmux2_1_y1, busmux2_1_y2, busmux2_1_y3, busmux2_2_y0, busmux2_2_y1, busmux2_2_y2,
       busmux2_2_y3, busmux2_3_y0, busmux2_3_y1, busmux2_3_y2, busmux2_3_y3, busmux2_4_y0, busmux2_4_y1,
       busmux2_4_y2, busmux2_4_y3, busmux2_5_y0, busmux2_5_y1, busmux2_5_y2, busmux2_5_y3, busmux2_6_y0,
       busmux2_6_y1, busmux2_6_y2, busmux2_6_y3, busmux2_7_y0, busmux2_7_y1, busmux2_7_y2, busmux2_7_y3,
       busmux2_8_y0, busmux2_8_y1, busmux2_8_y2, busmux2_8_y3, busmux2_9_y0, busmux2_9_y1, busmux2_9_y2,
       busmux2_9_y3, busmux2_10_y0, busmux2_10_y1, busmux2_10_y2, busmux2_10_y3, busmux2_11_y0,
       busmux2_11_y1, busmux2_11_y2, busmux2_11_y3, busmux2_12_y0, busmux2_12_y1, busmux2_12_y2,
       busmux2_12_y3, not_1_y, not_2_y, not_3_y, not_4_y, undriven, undriven_2, undriven_3, undriven_4,
       undriven_5, undriven_6, undriven_7, undriven_8, undriven_9, undriven_10, undriven_11, undriven_12,
       undriven_13, undriven_14, undriven_15, undriven_16, undriven_17, undriven_18, undriven_19,
       undriven_20, undriven_21, undriven_22, undriven_23, undriven_24, undriven_25, undriven_26,
       undriven_27, undriven_28, undriven_29, undriven_30, undriven_31, undriven_32, undriven_33,
       undriven_34, undriven_35, undriven_36, undriven_37, undriven_38, undriven_39, undriven_40,
       undriven_41, undriven_42, undriven_43, undriven_44, undriven_45, undriven_46, undriven_47,
       undriven_48, undriven_49, undriven_50, undriven_51, undriven_52, undriven_53, undriven_54,
       undriven_55, undriven_56, undriven_57, undriven_58, undriven_59, undriven_60, undriven_61,
       undriven_62, undriven_63, undriven_64, undriven_65, undriven_66, undriven_67, undriven_68;

  NOT not_1 (.A(N0), .Y(not_1_y));
  NOT not_2 (.A(N1), .Y(not_2_y));
  NOT not_3 (.A(N2), .Y(not_3_y));
  NOT not_4 (.A(N3), .Y(not_4_y));
  BUSMUX2 busmux2_1 (
    .a0(A0), .a1(A1), .a2(A2), .a3(A3), .b0(1'b0), .b1(A0), .b2(undriven_8), .b3(A2), .sA(not_1_y),
    .sB(undriven_3), .y0(busmux2_1_y0), .y1(busmux2_1_y1), .y2(busmux2_1_y2), .y3(busmux2_1_y3));
  BUSMUX2 busmux2_2 (
    .a0(A4), .a1(A5), .a2(A6), .a3(A7), .b0(A3), .b1(undriven_11), .b2(undriven_9), .b3(undriven_15),
    .sA(undriven_21), .sB(undriven_4), .y0(busmux2_2_y0), .y1(busmux2_2_y1), .y2(busmux2_2_y2),
    .y3(busmux2_2_y3));
  BUSMUX2 busmux2_3 (
    .a0(A8), .a1(A9), .a2(A10), .a3(A11), .b0(undriven_13), .b1(undriven_19), .b2(undriven_16),
    .b3(undriven_12), .sA(undriven_22), .sB(undriven_5), .y0(busmux2_3_y0), .y1(busmux2_3_y1),
    .y2(busmux2_3_y2), .y3(busmux2_3_y3));
  BUSMUX2 busmux2_4 (
    .a0(A12), .a1(A13), .a2(A14), .a3(A15), .b0(undriven_10), .b1(undriven_20), .b2(undriven_17),
    .b3(undriven_14), .sA(undriven_23), .sB(undriven_6), .y0(busmux2_4_y0), .y1(busmux2_4_y1),
    .y2(busmux2_4_y2), .y3(busmux2_4_y3));
  BUSMUX2 busmux2_5 (
    .a0(busmux2_1_y0), .a1(busmux2_1_y1), .a2(busmux2_1_y2), .a3(busmux2_1_y3), .b0(undriven_18),
    .b1(undriven_18), .b2(undriven_34), .b3(undriven_31), .sA(not_2_y), .sB(undriven_2), .y0(busmux2_5_y0),
    .y1(busmux2_5_y1), .y2(busmux2_5_y2), .y3(busmux2_5_y3));
  BUSMUX2 busmux2_6 (
    .a0(busmux2_2_y0), .a1(busmux2_2_y1), .a2(busmux2_2_y2), .a3(busmux2_2_y3), .b0(undriven_29),
    .b1(undriven_27), .b2(undriven_40), .b3(undriven_25), .sA(undriven_37), .sB(undriven_41),
    .y0(busmux2_6_y0), .y1(busmux2_6_y1), .y2(busmux2_6_y2), .y3(busmux2_6_y3));
  BUSMUX2 busmux2_7 (
    .a0(busmux2_3_y0), .a1(busmux2_3_y1), .a2(busmux2_3_y2), .a3(busmux2_3_y3), .b0(undriven_35),
    .b1(undriven_24), .b2(undriven_32), .b3(undriven_30), .sA(undriven_38), .sB(undriven_41),
    .y0(busmux2_7_y0), .y1(busmux2_7_y1), .y2(busmux2_7_y2), .y3(busmux2_7_y3));
  BUSMUX2 busmux2_8 (
    .a0(busmux2_4_y0), .a1(busmux2_4_y1), .a2(busmux2_4_y2), .a3(busmux2_4_y3), .b0(undriven_28),
    .b1(undriven_26), .b2(undriven_36), .b3(undriven_33), .sA(undriven_39), .sB(undriven_41),
    .y0(busmux2_8_y0), .y1(busmux2_8_y1), .y2(busmux2_8_y2), .y3(busmux2_8_y3));
  BUSMUX2 busmux2_9 (
    .a0(busmux2_5_y0), .a1(busmux2_5_y1), .a2(busmux2_5_y2), .a3(busmux2_5_y3), .b0(undriven_18),
    .b1(undriven_18), .b2(undriven_18), .b3(undriven_18), .sA(not_3_y), .sB(undriven_7), .y0(busmux2_9_y0),
    .y1(busmux2_9_y1), .y2(busmux2_9_y2), .y3(busmux2_9_y3));
  BUSMUX2 busmux2_10 (
    .a0(busmux2_6_y0), .a1(busmux2_6_y1), .a2(busmux2_6_y2), .a3(busmux2_6_y3), .b0(undriven_51),
    .b1(undriven_49), .b2(undriven_47), .b3(undriven_45), .sA(undriven_53), .sB(undriven_56),
    .y0(busmux2_10_y0), .y1(busmux2_10_y1), .y2(busmux2_10_y2), .y3(busmux2_10_y3));
  BUSMUX2 busmux2_11 (
    .a0(busmux2_7_y0), .a1(busmux2_7_y1), .a2(busmux2_7_y2), .a3(busmux2_7_y3), .b0(busmux2_6_y0),
    .b1(undriven_43), .b2(undriven_52), .b3(undriven_42), .sA(undriven_54), .sB(undriven_56),
    .y0(busmux2_11_y0), .y1(busmux2_11_y1), .y2(busmux2_11_y2), .y3(busmux2_11_y3));
  BUSMUX2 busmux2_12 (
    .a0(busmux2_8_y0), .a1(busmux2_8_y1), .a2(busmux2_8_y2), .a3(busmux2_8_y3), .b0(undriven_50),
    .b1(undriven_48), .b2(undriven_46), .b3(undriven_44), .sA(undriven_55), .sB(undriven_56),
    .y0(busmux2_12_y0), .y1(busmux2_12_y1), .y2(busmux2_12_y2), .y3(busmux2_12_y3));
  BUSMUX2 busmux2_13 (
    .a0(busmux2_9_y0), .a1(busmux2_9_y1), .a2(busmux2_9_y2), .a3(busmux2_9_y3), .b0(undriven_18),
    .b1(undriven_18), .b2(undriven_18), .b3(undriven_18), .sA(not_4_y), .sB(undriven), .y0(Y0), .y1(Y1),
    .y2(Y2), .y3(Y3));
  BUSMUX2 busmux2_14 (
    .a0(busmux2_10_y0), .a1(busmux2_10_y1), .a2(busmux2_10_y2), .a3(busmux2_10_y3), .b0(undriven_18),
    .b1(undriven_18), .b2(undriven_18), .b3(undriven_18), .sA(undriven_63), .sB(undriven), .y0(Y4), .y1(Y5),
    .y2(Y6), .y3(Y7));
  BUSMUX2 busmux2_15 (
    .a0(busmux2_11_y0), .a1(busmux2_11_y1), .a2(busmux2_11_y2), .a3(busmux2_11_y3), .b0(undriven_64),
    .b1(undriven_62), .b2(undriven_61), .b3(undriven_60), .sA(undriven_65), .sB(undriven_66), .y0(Y8),
    .y1(Y9), .y2(Y10), .y3(Y11));
  BUSMUX2 busmux2_16 (
    .a0(busmux2_12_y0), .a1(busmux2_12_y1), .a2(busmux2_12_y2), .a3(busmux2_12_y3), .b0(undriven_67),
    .b1(undriven_59), .b2(undriven_58), .b3(undriven_57), .sA(undriven_68), .sB(undriven_66), .y0(Y12),
    .y1(Y13), .y2(Y14), .y3(Y15));
endmodule

module RSHIFT16 (
  input  A0,
  input  N0,
  input  A1,
  input  N1,
  input  A2,
  input  N2,
  input  A3,
  input  N3,
  input  A4,
  input  A5,
  input  A6,
  input  A7,
  input  A8,
  input  A9,
  input  A10,
  input  A11,
  input  A12,
  input  A13,
  input  A14,
  input  A15,
  output Y0,
  output Y1,
  output Y2,
  output Y3,
  output Y4,
  output Y5,
  output Y6,
  output Y7,
  output Y8,
  output Y9,
  output Y10,
  output Y11,
  output Y12,
  output Y13,
  output Y14,
  output Y15
);

  wire busmux2_1_y0, busmux2_1_y1, busmux2_1_y2, busmux2_1_y3, busmux2_2_y0, busmux2_2_y1, busmux2_2_y2,
       busmux2_2_y3, busmux2_3_y0, busmux2_3_y1, busmux2_3_y2, busmux2_3_y3, busmux2_4_y0, busmux2_4_y1,
       busmux2_4_y2, busmux2_4_y3, busmux2_5_y0, busmux2_5_y1, busmux2_5_y2, busmux2_5_y3, busmux2_6_y0,
       busmux2_6_y1, busmux2_6_y2, busmux2_6_y3, busmux2_7_y0, busmux2_7_y1, busmux2_7_y2, busmux2_7_y3,
       busmux2_8_y0, busmux2_8_y1, busmux2_8_y2, busmux2_8_y3, busmux2_9_y0, busmux2_9_y1, busmux2_9_y2,
       busmux2_9_y3, busmux2_10_y0, busmux2_10_y1, busmux2_10_y2, busmux2_10_y3, busmux2_11_y0,
       busmux2_11_y1, busmux2_11_y2, busmux2_11_y3, busmux2_12_y0, busmux2_12_y1, busmux2_12_y2,
       busmux2_12_y3, not_1_y, not_2_y, not_3_y, not_4_y, undriven, undriven_2, undriven_3, undriven_4,
       undriven_5, undriven_6, undriven_7, undriven_8, undriven_9, undriven_10, undriven_11, undriven_12,
       undriven_13, undriven_14, undriven_15, undriven_16, undriven_17, undriven_18, undriven_19,
       undriven_20, undriven_21, undriven_22, undriven_23, undriven_24, undriven_25, undriven_26,
       undriven_27, undriven_28, undriven_29, undriven_30, undriven_31, undriven_32, undriven_33,
       undriven_34, undriven_35, undriven_36, undriven_37, undriven_38, undriven_39, undriven_40,
       undriven_41, undriven_42, undriven_43, undriven_44, undriven_45, undriven_46, undriven_47,
       undriven_48, undriven_49, undriven_50, undriven_51, undriven_52;

  NOT not_1 (.A(N0), .Y(not_1_y));
  NOT not_2 (.A(N1), .Y(not_2_y));
  NOT not_3 (.A(N2), .Y(not_3_y));
  NOT not_4 (.A(N3), .Y(not_4_y));
  BUSMUX2 busmux2_1 (
    .a0(A0), .a1(A1), .a2(A2), .a3(A3), .b0(undriven_14), .b1(undriven_8), .b2(undriven_18), .b3(A4),
    .sA(not_1_y), .sB(undriven_3), .y0(busmux2_1_y0), .y1(busmux2_1_y1), .y2(busmux2_1_y2), .y3(busmux2_1_y3));
  BUSMUX2 busmux2_2 (
    .a0(undriven_19), .a1(A5), .a2(A6), .a3(A7), .b0(A5), .b1(A6), .b2(undriven_9), .b3(A8),
    .sA(undriven_15), .sB(undriven_4), .y0(busmux2_2_y0), .y1(busmux2_2_y1), .y2(busmux2_2_y2),
    .y3(busmux2_2_y3));
  BUSMUX2 busmux2_3 (
    .a0(undriven_20), .a1(A9), .a2(A10), .a3(A11), .b0(undriven_21), .b1(undriven_12), .b2(undriven_10),
    .b3(A12), .sA(undriven_16), .sB(undriven_5), .y0(busmux2_3_y0), .y1(busmux2_3_y1), .y2(busmux2_3_y2),
    .y3(busmux2_3_y3));
  BUSMUX2 busmux2_4 (
    .a0(undriven_22), .a1(A13), .a2(A14), .a3(A15), .b0(undriven_23), .b1(undriven_13), .b2(undriven_11),
    .b3(1'b0), .sA(undriven_17), .sB(undriven_6), .y0(busmux2_4_y0), .y1(busmux2_4_y1), .y2(busmux2_4_y2),
    .y3(busmux2_4_y3));
  BUSMUX2 busmux2_5 (
    .a0(busmux2_1_y0), .a1(busmux2_1_y1), .a2(busmux2_1_y2), .a3(busmux2_1_y3), .b0(undriven_32),
    .b1(undriven_28), .b2(busmux2_2_y0), .b3(busmux2_2_y1), .sA(not_2_y), .sB(undriven_2), .y0(busmux2_5_y0),
    .y1(busmux2_5_y1), .y2(busmux2_5_y2), .y3(busmux2_5_y3));
  BUSMUX2 busmux2_6 (
    .a0(busmux2_2_y0), .a1(busmux2_2_y1), .a2(busmux2_2_y2), .a3(busmux2_2_y3), .b0(undriven_33),
    .b1(undriven_25), .b2(busmux2_3_y0), .b3(busmux2_3_y1), .sA(undriven_29), .sB(undriven_2),
    .y0(busmux2_6_y0), .y1(busmux2_6_y1), .y2(busmux2_6_y2), .y3(busmux2_6_y3));
  BUSMUX2 busmux2_7 (
    .a0(busmux2_3_y0), .a1(busmux2_3_y1), .a2(busmux2_3_y2), .a3(busmux2_3_y3), .b0(undriven_34),
    .b1(undriven_26), .b2(busmux2_4_y0), .b3(busmux2_4_y1), .sA(undriven_30), .sB(undriven_2),
    .y0(busmux2_7_y0), .y1(busmux2_7_y1), .y2(busmux2_7_y2), .y3(busmux2_7_y3));
  BUSMUX2 busmux2_8 (
    .a0(busmux2_4_y0), .a1(busmux2_4_y1), .a2(busmux2_4_y2), .a3(busmux2_4_y3), .b0(undriven_35),
    .b1(undriven_27), .b2(undriven_24), .b3(undriven_36), .sA(undriven_31), .sB(undriven_2),
    .y0(busmux2_8_y0), .y1(busmux2_8_y1), .y2(busmux2_8_y2), .y3(busmux2_8_y3));
  BUSMUX2 busmux2_9 (
    .a0(busmux2_5_y0), .a1(busmux2_5_y1), .a2(busmux2_5_y2), .a3(busmux2_5_y3), .b0(busmux2_6_y0),
    .b1(busmux2_6_y1), .b2(busmux2_6_y2), .b3(busmux2_6_y3), .sA(not_3_y), .sB(undriven_7),
    .y0(busmux2_9_y0), .y1(busmux2_9_y1), .y2(busmux2_9_y2), .y3(busmux2_9_y3));
  BUSMUX2 busmux2_10 (
    .a0(busmux2_6_y0), .a1(busmux2_6_y1), .a2(busmux2_6_y2), .a3(busmux2_6_y3), .b0(busmux2_7_y0),
    .b1(busmux2_7_y1), .b2(busmux2_7_y2), .b3(busmux2_7_y3), .sA(undriven_37), .sB(undriven_7),
    .y0(busmux2_10_y0), .y1(busmux2_10_y1), .y2(busmux2_10_y2), .y3(busmux2_10_y3));
  BUSMUX2 busmux2_11 (
    .a0(busmux2_7_y0), .a1(busmux2_7_y1), .a2(busmux2_7_y2), .a3(busmux2_7_y3), .b0(busmux2_8_y0),
    .b1(busmux2_8_y1), .b2(busmux2_8_y2), .b3(busmux2_8_y3), .sA(undriven_38), .sB(undriven_7),
    .y0(busmux2_11_y0), .y1(busmux2_11_y1), .y2(busmux2_11_y2), .y3(busmux2_11_y3));
  BUSMUX2 busmux2_12 (
    .a0(busmux2_8_y0), .a1(busmux2_8_y1), .a2(busmux2_8_y2), .a3(busmux2_8_y3), .b0(undriven_24),
    .b1(undriven_40), .b2(undriven_41), .b3(undriven_42), .sA(undriven_39), .sB(undriven_7),
    .y0(busmux2_12_y0), .y1(busmux2_12_y1), .y2(busmux2_12_y2), .y3(busmux2_12_y3));
  BUSMUX2 busmux2_13 (
    .a0(busmux2_9_y0), .a1(busmux2_9_y1), .a2(busmux2_9_y2), .a3(busmux2_9_y3), .b0(busmux2_11_y0),
    .b1(busmux2_11_y1), .b2(busmux2_11_y2), .b3(busmux2_11_y3), .sA(not_4_y), .sB(undriven), .y0(Y0),
    .y1(Y1), .y2(Y2), .y3(Y3));
  BUSMUX2 busmux2_14 (
    .a0(busmux2_10_y0), .a1(busmux2_10_y1), .a2(busmux2_10_y2), .a3(busmux2_10_y3), .b0(busmux2_12_y0),
    .b1(busmux2_12_y1), .b2(busmux2_12_y2), .b3(busmux2_12_y3), .sA(undriven_43), .sB(undriven), .y0(Y4),
    .y1(Y5), .y2(Y6), .y3(Y7));
  BUSMUX2 busmux2_15 (
    .a0(busmux2_11_y0), .a1(busmux2_11_y1), .a2(busmux2_11_y2), .a3(busmux2_11_y3), .b0(undriven_24),
    .b1(undriven_46), .b2(undriven_47), .b3(undriven_48), .sA(undriven_44), .sB(undriven), .y0(Y8), .y1(Y9),
    .y2(Y10), .y3(Y11));
  BUSMUX2 busmux2_16 (
    .a0(busmux2_12_y0), .a1(busmux2_12_y1), .a2(busmux2_12_y2), .a3(busmux2_12_y3), .b0(undriven_49),
    .b1(undriven_50), .b2(undriven_51), .b3(undriven_52), .sA(undriven_45), .sB(undriven), .y0(Y12),
    .y1(Y13), .y2(Y14), .y3(Y15));
endmodule

module MUX1_16 (
  input  d0,
  input  d1,
  input  d2,
  input  d3,
  input  d4,
  input  d5,
  input  d6,
  input  d7,
  input  d8,
  input  d9,
  input  d10,
  input  d11,
  input  d12,
  input  d13,
  input  d14,
  input  d15,
  input  s0,
  input  s1,
  input  s2,
  input  s3,
  input  s4,
  input  s5,
  input  s6,
  input  s7,
  input  s8,
  input  s9,
  input  s10,
  input  s11,
  input  s12,
  input  s13,
  input  s14,
  input  s15,
  output Y
);

  wire and_1_y, and_2_y, and_3_y, and_4_y, and_5_y, and_6_y, and_7_y, and_8_y, and_9_y, and_10_y, and_11_y,
       and_12_y, and_13_y, and_14_y, and_15_y, and_16_y;

  AND and_1 (.A(d0), .B(s0), .Y(and_1_y));
  AND and_2 (.A(d1), .B(s1), .Y(and_2_y));
  AND and_3 (.A(d2), .B(s2), .Y(and_3_y));
  AND and_4 (.A(d3), .B(s3), .Y(and_4_y));
  AND and_5 (.A(d4), .B(s4), .Y(and_5_y));
  AND and_6 (.A(d5), .B(s5), .Y(and_6_y));
  AND and_7 (.A(d6), .B(s6), .Y(and_7_y));
  AND and_8 (.A(d7), .B(s7), .Y(and_8_y));
  AND and_9 (.A(d8), .B(s8), .Y(and_9_y));
  AND and_10 (.A(d9), .B(s9), .Y(and_10_y));
  AND and_11 (.A(d10), .B(s10), .Y(and_11_y));
  AND and_12 (.A(d11), .B(s11), .Y(and_12_y));
  AND and_13 (.A(d12), .B(s12), .Y(and_13_y));
  AND and_14 (.A(d13), .B(s13), .Y(and_14_y));
  AND and_15 (.A(d14), .B(s14), .Y(and_15_y));
  AND and_16 (.A(d15), .B(s15), .Y(and_16_y));
  OR16 or16_1 (
    .i0(and_1_y), .i1(and_2_y), .i2(and_3_y), .i3(and_4_y), .i4(and_5_y), .i5(and_6_y), .i6(and_7_y),
    .i7(and_8_y), .i8(and_9_y), .i9(and_10_y), .i10(and_11_y), .i11(and_12_y), .i12(and_13_y),
    .i13(and_14_y), .i14(and_15_y), .i15(and_16_y), .Y(Y));
endmodule

module BUSMUX2 (
  input  a0,
  input  a1,
  input  a2,
  input  a3,
  input  b0,
  input  b1,
  input  b2,
  input  b3,
  input  sA,
  input  sB,
  output y0,
  output y1,
  output y2,
  output y3
);

  wire and_1_y, and_2_y, and_3_y, and_4_y, and_5_y, and_6_y, and_7_y, and_8_y, undriven, undriven_2,
       undriven_3, undriven_4, undriven_5, undriven_6;

  AND and_1 (.A(a0), .B(sA), .Y(and_1_y));
  AND and_2 (.A(b0), .B(sB), .Y(and_2_y));
  OR or_1 (.A(and_1_y), .B(and_2_y), .Y(y0));
  AND and_3 (.A(a1), .B(undriven), .Y(and_3_y));
  AND and_4 (.A(b1), .B(undriven_2), .Y(and_4_y));
  OR or_2 (.A(and_3_y), .B(and_4_y), .Y(y1));
  AND and_5 (.A(a2), .B(undriven_3), .Y(and_5_y));
  AND and_6 (.A(b2), .B(undriven_4), .Y(and_6_y));
  OR or_3 (.A(and_5_y), .B(and_6_y), .Y(y2));
  AND and_7 (.A(a3), .B(undriven_5), .Y(and_7_y));
  AND and_8 (.A(b3), .B(undriven_6), .Y(and_8_y));
  OR or_4 (.A(and_7_y), .B(and_8_y), .Y(y3));
endmodule

module ADD8 (
  input  A0,
  input  A1,
  input  A2,
  input  A3,
  input  A4,
  input  A5,
  input  A6,
  input  A7,
  input  B0,
  input  B1,
  input  B2,
  input  B3,
  input  B4,
  input  B5,
  input  B6,
  input  B7,
  input  Cin,
  output S0,
  output S1,
  output S2,
  output S3,
  output S4,
  output S5,
  output S6,
  output S7,
  output Cout
);

  wire fulladd_1_cout, fulladd_2_cout, fulladd_3_cout, fulladd_4_cout, fulladd_5_cout, fulladd_6_cout,
       fulladd_7_cout;

  FULLADD fulladd_1 (.A(A0), .B(B0), .Cin(Cin), .S(S0), .Cout(fulladd_1_cout));
  FULLADD fulladd_2 (.A(A1), .B(B1), .Cin(fulladd_1_cout), .S(S1), .Cout(fulladd_2_cout));
  FULLADD fulladd_3 (.A(A2), .B(B2), .Cin(fulladd_2_cout), .S(S2), .Cout(fulladd_3_cout));
  FULLADD fulladd_4 (.A(A3), .B(B3), .Cin(fulladd_3_cout), .S(S3), .Cout(fulladd_4_cout));
  FULLADD fulladd_5 (.A(A4), .B(B4), .Cin(fulladd_4_cout), .S(S4), .Cout(fulladd_5_cout));
  FULLADD fulladd_6 (.A(A5), .B(B5), .Cin(fulladd_5_cout), .S(S5), .Cout(fulladd_6_cout));
  FULLADD fulladd_7 (.A(A6), .B(B6), .Cin(fulladd_6_cout), .S(S6), .Cout(fulladd_7_cout));
  FULLADD fulladd_8 (.A(A7), .B(B7), .Cin(fulladd_7_cout), .S(S7), .Cout(Cout));
endmodule

module AND8 (
  input  A0,
  input  A1,
  input  A2,
  input  A3,
  input  A4,
  input  A5,
  input  A6,
  input  A7,
  input  B0,
  input  B1,
  input  B2,
  input  B3,
  input  B4,
  input  B5,
  input  B6,
  input  B7,
  output Y0,
  output Y1,
  output Y2,
  output Y3,
  output Y4,
  output Y5,
  output Y6,
  output Y7
);

  AND and_1 (.A(A0), .B(B0), .Y(Y0));
  AND and_2 (.A(A1), .B(B1), .Y(Y1));
  AND and_3 (.A(A2), .B(B2), .Y(Y2));
  AND and_4 (.A(A3), .B(B3), .Y(Y3));
  AND and_5 (.A(A4), .B(B4), .Y(Y4));
  AND and_6 (.A(A5), .B(B5), .Y(Y5));
  AND and_7 (.A(A6), .B(B6), .Y(Y6));
  AND and_8 (.A(A7), .B(B7), .Y(Y7));
endmodule

module XOR8 (
  input  A0,
  input  A1,
  input  A2,
  input  A3,
  input  A4,
  input  A5,
  input  A6,
  input  A7,
  input  B0,
  input  B1,
  input  B2,
  input  B3,
  input  B4,
  input  B5,
  input  B6,
  input  B7,
  output Y0,
  output Y1,
  output Y2,
  output Y3,
  output Y4,
  output Y5,
  output Y6,
  output Y7
);

  XOR xor_1 (.A(A0), .B(B0), .Y(Y0));
  XOR xor_2 (.A(A1), .B(B1), .Y(Y1));
  XOR xor_3 (.A(A2), .B(B2), .Y(Y2));
  XOR xor_4 (.A(A3), .B(B3), .Y(Y3));
  XOR xor_5 (.A(A4), .B(B4), .Y(Y4));
  XOR xor_6 (.A(A5), .B(B5), .Y(Y5));
  XOR xor_7 (.A(A6), .B(B6), .Y(Y6));
  XOR xor_8 (.A(A7), .B(B7), .Y(Y7));
endmodule

module FULLADD (
  input  A,
  input  B,
  input  Cin,
  output S,
  output Cout
);

  wire undriven, undriven_2, undriven_3;

  ODD odd_1 (.A(A), .B(B), .Cin(Cin), .Y(S));
  MAJ maj_1 (.A(undriven), .B(undriven_2), .Cin(undriven_3), .Y(Cout));
endmodule

module MAJ (
  input  A,
  input  B,
  input  Cin,
  output Y
);

  wire and_1_y, and_2_y, and_3_y, undriven, undriven_2, undriven_3;

  AND and_1 (.A(A), .B(B), .Y(and_1_y));
  AND and_2 (.A(undriven), .B(Cin), .Y(and_2_y));
  AND and_3 (.A(undriven_2), .B(undriven_3), .Y(and_3_y));
  OR3 or3_1 (.A(and_1_y), .B(and_2_y), .C(and_3_y), .Y(Y));
endmodule

module ODD (
  input  A,
  input  B,
  input  Cin,
  output Y
);

  wire xor_1_y;

  XOR xor_1 (.A(A), .B(B), .Y(xor_1_y));
  XOR xor_2 (.A(xor_1_y), .B(Cin), .Y(Y));
endmodule

module AND (
  input  A,
  input  B,
  output Y
);

  wire nand_1_y;

  NAND nand_1 (.A(A), .B(B), .Y(nand_1_y));
  NOT not_1 (.A(nand_1_y), .Y(Y));
endmodule

module OR (
  input  A,
  input  B,
  output Y
);

  wire nor_1_y;

  NOR nor_1 (.A(A), .B(B), .Y(nor_1_y));
  NOT not_1 (.A(nor_1_y), .Y(Y));
endmodule

module OR3 (
  input  A,
  input  B,
  input  C,
  output Y
);

  wire or_1_y;

  OR or_1 (.A(A), .B(B), .Y(or_1_y));
  OR or_2 (.A(or_1_y), .B(C), .Y(Y));
endmodule

module XOR (
  input  A,
  input  B,
  output Y
);

  wire nand_1_y, nand_2_y, nand_3_y, undriven, undriven_2, undriven_3, undriven_4;

  NAND nand_1 (.A(undriven_3), .B(undriven), .Y(nand_1_y));
  NAND nand_2 (.A(A), .B(undriven_4), .Y(nand_2_y));
  NAND nand_3 (.A(undriven_2), .B(nand_1_y), .Y(nand_3_y));
  NAND nand_4 (.A(nand_2_y), .B(nand_3_y), .Y(Y));
endmodule

module NOT (
  input  A,
  output Y
);

  Transistor #(.\type ("p")) transistor_1 (.in(1'b1), .out(Y), .gate(A));
  Transistor #(.\type ("n")) transistor_2 (.in(1'b0), .out(Y), .gate(A));
endmodule

module NAND (
  input  A,
  input  B,
  output Y
);

  wire transistor_4_out, undriven, undriven_2;

  Transistor #(.\type ("p")) transistor_1 (.in(1'b1), .out(Y), .gate(undriven));
  Transistor #(.\type ("p")) transistor_2 (.in(1'b1), .out(Y), .gate(undriven_2));
  Transistor #(.\type ("n")) transistor_3 (.in(transistor_4_out), .out(Y), .gate(B));
  Transistor #(.\type ("n")) transistor_4 (.in(1'b0), .out(transistor_4_out), .gate(A));
endmodule

module NOR (
  input  A,
  input  B,
  output Y
);

  wire transistor_1_out, undriven, undriven_2;

  Transistor #(.\type ("p")) transistor_1 (.in(1'b1), .out(transistor_1_out), .gate(undriven));
  Transistor #(.\type ("p")) transistor_2 (.in(transistor_1_out), .out(Y), .gate(undriven_2));
  Transistor #(.\type ("n")) transistor_3 (.in(1'b0), .out(Y), .gate(A));
  Transistor #(.\type ("n")) transistor_4 (.in(1'b0), .out(Y), .gate(B));
endmodule

module SRLATCH (
  input  S,
  input  R,
  output Q,
  output Qb
);

  wire nor_1_y, nor_2_y;

  NOR nor_1 (.A(R), .B(Qb), .Y(nor_1_y));
  NOR nor_2 (.A(S), .B(Q), .Y(nor_2_y));
endmodule

module MEMBIT (
  input  D,
  input  WRITE,
  output Q
);

  wire and_1_y, and_2_y, not_1_y, undriven, undriven_2;

  NOT not_1 (.A(D), .Y(not_1_y));
  AND and_1 (.A(undriven), .B(WRITE), .Y(and_1_y));
  AND and_2 (.A(not_1_y), .B(undriven_2), .Y(and_2_y));
  SRLATCH srlatch_1 (.S(and_1_y), .R(and_2_y), .Q(Q));  // open: Qb
endmodule
module MEMORY16 (
  input  A0,
  input  A1,
  input  A2,
  input  A3,
  input  D0,
  input  D1,
  input  D2,
  input  D3,
  input  D4,
  input  D5,
  input  D6,
  input  D7,
  input  D8,
  input  D9,
  input  D10,
  input  D11,
  input  D12,
  input  D13,
  input  D14,
  input  D15,
  input  WRITE,
  output Q0,
  output Q1,
  output Q2,
  output Q3,
  output Q4,
  output Q5,
  output Q6,
  output Q7,
  output Q8,
  output Q9,
  output Q10,
  output Q11,
  output Q12,
  output Q13,
  output Q14,
  output Q15
);

  wire and_1_out, and_2_out, and_3_out, and_4_out, and_5_out, and_6_out, and_7_out, and_8_out, and_9_out,
       and_10_out, and_11_out, and_12_out, and_13_out, and_14_out, and_15_out, and_16_out, decoder4b_1_d0,
       decoder4b_1_d1, decoder4b_1_d2, decoder4b_1_d3, decoder4b_1_d4, decoder4b_1_d5, decoder4b_1_d6,
       decoder4b_1_d7, decoder4b_1_d8, decoder4b_1_d9, decoder4b_1_d10, decoder4b_1_d11, decoder4b_1_d12,
       decoder4b_1_d13, decoder4b_1_d14, decoder4b_1_d15, membit_1_q, membit_2_q, membit_3_q, membit_4_q,
       membit_5_q, membit_6_q, membit_7_q, membit_8_q, membit_9_q, membit_10_q, membit_11_q, membit_12_q,
       membit_13_q, membit_14_q, membit_15_q, membit_16_q, membit_17_q, membit_18_q, membit_19_q,
       membit_20_q, membit_21_q, membit_22_q, membit_23_q, membit_24_q, membit_25_q, membit_26_q,
       membit_27_q, membit_28_q, membit_29_q, membit_30_q, membit_31_q, membit_32_q, membit_33_q,
       membit_34_q, membit_35_q, membit_36_q, membit_37_q, membit_38_q, membit_39_q, membit_40_q,
       membit_41_q, membit_42_q, membit_43_q, membit_44_q, membit_45_q, membit_46_q, membit_47_q,
       membit_48_q, membit_49_q, membit_50_q, membit_51_q, membit_52_q, membit_53_q, membit_54_q,
       membit_55_q, membit_56_q, membit_57_q, membit_58_q, membit_59_q, membit_60_q, membit_61_q,
       membit_62_q, membit_63_q, membit_64_q, membit_65_q, membit_66_q, membit_67_q, membit_68_q,
       membit_69_q, membit_70_q, membit_71_q, membit_72_q, membit_73_q, membit_74_q, membit_75_q,
       membit_76_q, membit_77_q, membit_78_q, membit_79_q, membit_80_q, membit_81_q, membit_82_q,
       membit_83_q, membit_84_q, membit_85_q, membit_86_q, membit_87_q, membit_88_q, membit_89_q,
       membit_90_q, membit_91_q, membit_92_q, membit_93_q, membit_94_q, membit_95_q, membit_96_q,
       membit_97_q, membit_98_q, membit_99_q, membit_100_q, membit_101_q, membit_102_q, membit_103_q,
       membit_104_q, membit_105_q, membit_106_q, membit_107_q, membit_108_q, membit_109_q, membit_110_q,
       membit_111_q, membit_112_q, membit_113_q, membit_114_q, membit_115_q, membit_116_q, membit_117_q,
       membit_118_q, membit_119_q, membit_120_q, membit_121_q, membit_122_q, membit_123_q, membit_124_q,
       membit_125_q, membit_126_q, membit_127_q, membit_128_q, membit_129_q, membit_130_q, membit_131_q,
       membit_132_q, membit_133_q, membit_134_q, membit_135_q, membit_136_q, membit_137_q, membit_138_q,
       membit_139_q, membit_140_q, membit_141_q, membit_142_q, membit_143_q, membit_144_q, membit_145_q,
       membit_146_q, membit_147_q, membit_148_q, membit_149_q, membit_150_q, membit_151_q, membit_152_q,
       membit_153_q, membit_154_q, membit_155_q, membit_156_q, membit_157_q, membit_158_q, membit_159_q,
       membit_160_q, membit_161_q, membit_162_q, membit_163_q, membit_164_q, membit_165_q, membit_166_q,
       membit_167_q, membit_168_q, membit_169_q, membit_170_q, membit_171_q, membit_172_q, membit_173_q,
       membit_174_q, membit_175_q, membit_176_q, membit_177_q, membit_178_q, membit_179_q, membit_180_q,
       membit_181_q, membit_182_q, membit_183_q, membit_184_q, membit_185_q, membit_186_q, membit_187_q,
       membit_188_q, membit_189_q, membit_190_q, membit_191_q, membit_192_q, membit_193_q, membit_194_q,
       membit_195_q, membit_196_q, membit_197_q, membit_198_q, membit_199_q, membit_200_q, membit_201_q,
       membit_202_q, membit_203_q, membit_204_q, membit_205_q, membit_206_q, membit_207_q, membit_208_q,
       membit_209_q, membit_210_q, membit_211_q, membit_212_q, membit_213_q, membit_214_q, membit_215_q,
       membit_216_q, membit_217_q, membit_218_q, membit_219_q, membit_220_q, membit_221_q, membit_222_q,
       membit_223_q, membit_224_q, membit_225_q, membit_226_q, membit_227_q, membit_228_q, membit_229_q,
       membit_230_q, membit_231_q, membit_232_q, membit_233_q, membit_234_q, membit_235_q, membit_236_q,
       membit_237_q, membit_238_q, membit_239_q, membit_240_q, membit_241_q, membit_242_q, membit_243_q,
       membit_244_q, membit_245_q, membit_246_q, membit_247_q, membit_248_q, membit_249_q, membit_250_q,
       membit_251_q, membit_252_q, membit_253_q, membit_254_q, membit_255_q, membit_256_q, undriven,
       undriven_2, undriven_3, undriven_4, undriven_5, undriven_6, undriven_7, undriven_8, undriven_9,
       undriven_10, undriven_11, undriven_12, undriven_13, undriven_14, undriven_15, undriven_16,
       undriven_17, undriven_18, undriven_19, undriven_20, undriven_21, undriven_22, undriven_23,
       undriven_24, undriven_25, undriven_26, undriven_27, undriven_28, undriven_29, undriven_30,
       undriven_31, undriven_32, undriven_33, undriven_34, undriven_35;

  DECODER4B decoder4b_1 (
    .S0(A0), .S1(A1), .S2(A2), .S3(A3), .D0(decoder4b_1_d0), .D1(decoder4b_1_d1), .D2(decoder4b_1_d2),
    .D3(decoder4b_1_d3), .D4(decoder4b_1_d4), .D5(decoder4b_1_d5), .D6(decoder4b_1_d6), .D7(decoder4b_1_d7),
    .D8(decoder4b_1_d8), .D9(decoder4b_1_d9), .D10(decoder4b_1_d10), .D11(decoder4b_1_d11),
    .D12(decoder4b_1_d12), .D13(decoder4b_1_d13), .D14(decoder4b_1_d14), .D15(decoder4b_1_d15));
  and and_1 (and_1_out, decoder4b_1_d0, WRITE);
  and and_2 (and_2_out, decoder4b_1_d1, undriven);
  and and_3 (and_3_out, decoder4b_1_d2, undriven);
  and and_4 (and_4_out, decoder4b_1_d3, undriven);
  and and_5 (and_5_out, decoder4b_1_d4, undriven);
  and and_6 (and_6_out, decoder4b_1_d5, undriven);
  and and_7 (and_7_out, decoder4b_1_d6, undriven_17);
  and and_8 (and_8_out, decoder4b_1_d7, undriven_15);
  and and_9 (and_9_out, decoder4b_1_d8, undriven_12);
  and and_10 (and_10_out, decoder4b_1_d9, undriven_13);
  and and_11 (and_11_out, decoder4b_1_d10, undriven_10);
  and and_12 (and_12_out, decoder4b_1_d11, undriven_7);
  and and_13 (and_13_out, decoder4b_1_d12, undriven_8);
  and and_14 (and_14_out, decoder4b_1_d13, undriven_5);
  and and_15 (and_15_out, decoder4b_1_d14, undriven_2);
  and and_16 (and_16_out, decoder4b_1_d15, undriven_3);
  MEMBIT membit_1 (.D(D0), .WRITE(and_1_out), .Q(membit_1_q));
  MEMBIT membit_2 (.D(D0), .WRITE(and_2_out), .Q(membit_2_q));
  MEMBIT membit_3 (.D(D0), .WRITE(and_3_out), .Q(membit_3_q));
  MEMBIT membit_4 (.D(D0), .WRITE(and_4_out), .Q(membit_4_q));
  MEMBIT membit_5 (.D(D0), .WRITE(and_5_out), .Q(membit_5_q));
  MEMBIT membit_6 (.D(D0), .WRITE(and_6_out), .Q(membit_6_q));
  MEMBIT membit_7 (.D(D0), .WRITE(and_7_out), .Q(membit_7_q));
  MEMBIT membit_8 (.D(D0), .WRITE(and_8_out), .Q(membit_8_q));
  MEMBIT membit_9 (.D(D0), .WRITE(and_9_out), .Q(membit_9_q));
  MEMBIT membit_10 (.D(D0), .WRITE(and_10_out), .Q(membit_10_q));
  MEMBIT membit_11 (.D(D0), .WRITE(and_11_out), .Q(membit_11_q));
  MEMBIT membit_12 (.D(D0), .WRITE(and_12_out), .Q(membit_12_q));
  MEMBIT membit_13 (.D(D0), .WRITE(and_13_out), .Q(membit_13_q));
  MEMBIT membit_14 (.D(D0), .WRITE(and_14_out), .Q(membit_14_q));
  MEMBIT membit_15 (.D(D0), .WRITE(and_15_out), .Q(membit_15_q));
  MEMBIT membit_16 (.D(D0), .WRITE(and_16_out), .Q(membit_16_q));
  MUX1_16 mux1_16_1 (
    .d0(membit_1_q), .d1(membit_2_q), .d2(membit_3_q), .d3(membit_4_q), .d4(membit_5_q), .d5(membit_6_q),
    .d6(membit_7_q), .d7(membit_8_q), .d8(membit_9_q), .d9(membit_10_q), .d10(membit_11_q),
    .d11(membit_12_q), .d12(membit_13_q), .d13(membit_14_q), .d14(membit_15_q), .d15(membit_16_q),
    .s0(decoder4b_1_d0), .s1(decoder4b_1_d1), .s2(decoder4b_1_d2), .s3(decoder4b_1_d3), .s4(decoder4b_1_d4),
    .s5(decoder4b_1_d5), .s6(undriven_18), .s7(undriven_16), .s8(decoder4b_1_d8), .s9(undriven_14),
    .s10(undriven_11), .s11(decoder4b_1_d11), .s12(undriven_9), .s13(undriven_6), .s14(decoder4b_1_d14),
    .s15(undriven_4), .Y(Q0));
  MEMBIT membit_17 (.D(D1), .WRITE(and_1_out), .Q(membit_17_q));
  MEMBIT membit_18 (.D(D1), .WRITE(and_2_out), .Q(membit_18_q));
  MEMBIT membit_19 (.D(D1), .WRITE(and_3_out), .Q(membit_19_q));
  MEMBIT membit_20 (.D(D1), .WRITE(and_4_out), .Q(membit_20_q));
  MEMBIT membit_21 (.D(D1), .WRITE(and_5_out), .Q(membit_21_q));
  MEMBIT membit_22 (.D(D1), .WRITE(and_6_out), .Q(membit_22_q));
  MEMBIT membit_23 (.D(D1), .WRITE(and_7_out), .Q(membit_23_q));
  MEMBIT membit_24 (.D(D1), .WRITE(and_8_out), .Q(membit_24_q));
  MEMBIT membit_25 (.D(D1), .WRITE(and_9_out), .Q(membit_25_q));
  MEMBIT membit_26 (.D(D1), .WRITE(and_10_out), .Q(membit_26_q));
  MEMBIT membit_27 (.D(D1), .WRITE(and_11_out), .Q(membit_27_q));
  MEMBIT membit_28 (.D(D1), .WRITE(and_12_out), .Q(membit_28_q));
  MEMBIT membit_29 (.D(D1), .WRITE(and_13_out), .Q(membit_29_q));
  MEMBIT membit_30 (.D(D1), .WRITE(and_14_out), .Q(membit_30_q));
  MEMBIT membit_31 (.D(D1), .WRITE(and_15_out), .Q(membit_31_q));
  MEMBIT membit_32 (.D(D1), .WRITE(undriven_34), .Q(membit_32_q));
  MUX1_16 mux1_16_2 (
    .d0(membit_17_q), .d1(membit_18_q), .d2(membit_19_q), .d3(membit_20_q), .d4(membit_21_q),
    .d5(membit_22_q), .d6(membit_23_q), .d7(membit_24_q), .d8(membit_25_q), .d9(membit_26_q),
    .d10(membit_27_q), .d11(membit_28_q), .d12(membit_29_q), .d13(membit_30_q), .d14(membit_31_q),
    .d15(membit_32_q), .s0(undriven_35), .s1(undriven_33), .s2(undriven_32), .s3(undriven_31),
    .s4(undriven_30), .s5(undriven_29), .s6(undriven_28), .s7(undriven_27), .s8(undriven_26),
    .s9(undriven_25), .s10(undriven_24), .s11(undriven_23), .s12(undriven_22), .s13(undriven_21),
    .s14(undriven_20), .s15(undriven_19), .Y(Q1));
  MEMBIT membit_33 (.D(D2), .WRITE(and_1_out), .Q(membit_33_q));
  MEMBIT membit_34 (.D(D2), .WRITE(and_2_out), .Q(membit_34_q));
  MEMBIT membit_35 (.D(D2), .WRITE(and_3_out), .Q(membit_35_q));
  MEMBIT membit_36 (.D(D2), .WRITE(and_4_out), .Q(membit_36_q));
  MEMBIT membit_37 (.D(D2), .WRITE(and_5_out), .Q(membit_37_q));
  MEMBIT membit_38 (.D(D2), .WRITE(and_6_out), .Q(membit_38_q));
  MEMBIT membit_39 (.D(D2), .WRITE(and_7_out), .Q(membit_39_q));
  MEMBIT membit_40 (.D(D2), .WRITE(and_8_out), .Q(membit_40_q));
  MEMBIT membit_41 (.D(D2), .WRITE(and_9_out), .Q(membit_41_q));
  MEMBIT membit_42 (.D(D2), .WRITE(and_10_out), .Q(membit_42_q));
  MEMBIT membit_43 (.D(D2), .WRITE(and_11_out), .Q(membit_43_q));
  MEMBIT membit_44 (.D(D2), .WRITE(and_12_out), .Q(membit_44_q));
  MEMBIT membit_45 (.D(D2), .WRITE(and_13_out), .Q(membit_45_q));
  MEMBIT membit_46 (.D(D2), .WRITE(and_14_out), .Q(membit_46_q));
  MEMBIT membit_47 (.D(D2), .WRITE(and_15_out), .Q(membit_47_q));
  MEMBIT membit_48 (.D(D2), .WRITE(undriven_34), .Q(membit_48_q));
  MUX1_16 mux1_16_3 (
    .d0(membit_33_q), .d1(membit_34_q), .d2(membit_35_q), .d3(membit_36_q), .d4(membit_37_q),
    .d5(membit_38_q), .d6(membit_39_q), .d7(membit_40_q), .d8(membit_41_q), .d9(membit_42_q),
    .d10(membit_43_q), .d11(membit_44_q), .d12(membit_45_q), .d13(membit_46_q), .d14(membit_47_q),
    .d15(membit_48_q), .s0(undriven_35), .s1(undriven_33), .s2(undriven_32), .s3(undriven_31),
    .s4(undriven_30), .s5(undriven_29), .s6(undriven_28), .s7(undriven_27), .s8(undriven_26),
    .s9(undriven_25), .s10(undriven_24), .s11(undriven_23), .s12(undriven_22), .s13(undriven_21),
    .s14(undriven_20), .s15(undriven_19), .Y(Q2));
  MEMBIT membit_49 (.D(D3), .WRITE(and_1_out), .Q(membit_49_q));
  MEMBIT membit_50 (.D(D3), .WRITE(and_2_out), .Q(membit_50_q));
  MEMBIT membit_51 (.D(D3), .WRITE(and_3_out), .Q(membit_51_q));
  MEMBIT membit_52 (.D(D3), .WRITE(and_4_out), .Q(membit_52_q));
  MEMBIT membit_53 (.D(D3), .WRITE(and_5_out), .Q(membit_53_q));
  MEMBIT membit_54 (.D(D3), .WRITE(and_6_out), .Q(membit_54_q));
  MEMBIT membit_55 (.D(D3), .WRITE(and_7_out), .Q(membit_55_q));
  MEMBIT membit_56 (.D(D3), .WRITE(and_8_out), .Q(membit_56_q));
  MEMBIT membit_57 (.D(D3), .WRITE(and_9_out), .Q(membit_57_q));
  MEMBIT membit_58 (.D(D3), .WRITE(and_10_out), .Q(membit_58_q));
  MEMBIT membit_59 (.D(D3), .WRITE(and_11_out), .Q(membit_59_q));
  MEMBIT membit_60 (.D(D3), .WRITE(and_12_out), .Q(membit_60_q));
  MEMBIT membit_61 (.D(D3), .WRITE(and_13_out), .Q(membit_61_q));
  MEMBIT membit_62 (.D(D3), .WRITE(and_14_out), .Q(membit_62_q));
  MEMBIT membit_63 (.D(D3), .WRITE(and_15_out), .Q(membit_63_q));
  MEMBIT membit_64 (.D(D3), .WRITE(undriven_34), .Q(membit_64_q));
  MUX1_16 mux1_16_4 (
    .d0(membit_49_q), .d1(membit_50_q), .d2(membit_51_q), .d3(membit_52_q), .d4(membit_53_q),
    .d5(membit_54_q), .d6(membit_55_q), .d7(membit_56_q), .d8(membit_57_q), .d9(membit_58_q),
    .d10(membit_59_q), .d11(membit_60_q), .d12(membit_61_q), .d13(membit_62_q), .d14(membit_63_q),
    .d15(membit_64_q), .s0(undriven_35), .s1(undriven_33), .s2(undriven_32), .s3(undriven_31),
    .s4(undriven_30), .s5(undriven_29), .s6(undriven_28), .s7(undriven_27), .s8(undriven_26),
    .s9(undriven_25), .s10(undriven_24), .s11(undriven_23), .s12(undriven_22), .s13(undriven_21),
    .s14(undriven_20), .s15(undriven_19), .Y(Q3));
  MEMBIT membit_65 (.D(D4), .WRITE(and_1_out), .Q(membit_65_q));
  MEMBIT membit_66 (.D(D4), .WRITE(and_2_out), .Q(membit_66_q));
  MEMBIT membit_67 (.D(D4), .WRITE(and_3_out), .Q(membit_67_q));
  MEMBIT membit_68 (.D(D4), .WRITE(and_4_out), .Q(membit_68_q));
  MEMBIT membit_69 (.D(D4), .WRITE(and_5_out), .Q(membit_69_q));
  MEMBIT membit_70 (.D(D4), .WRITE(and_6_out), .Q(membit_70_q));
  MEMBIT membit_71 (.D(D4), .WRITE(and_7_out), .Q(membit_71_q));
  MEMBIT membit_72 (.D(D4), .WRITE(and_8_out), .Q(membit_72_q));
  MEMBIT membit_73 (.D(D4), .WRITE(and_9_out), .Q(membit_73_q));
  MEMBIT membit_74 (.D(D4), .WRITE(and_10_out), .Q(membit_74_q));
  MEMBIT membit_75 (.D(D4), .WRITE(and_11_out), .Q(membit_75_q));
  MEMBIT membit_76 (.D(D4), .WRITE(and_12_out), .Q(membit_76_q));
  MEMBIT membit_77 (.D(D4), .WRITE(and_13_out), .Q(membit_77_q));
  MEMBIT membit_78 (.D(D4), .WRITE(and_14_out), .Q(membit_78_q));
  MEMBIT membit_79 (.D(D4), .WRITE(and_15_out), .Q(membit_79_q));
  MEMBIT membit_80 (.D(D4), .WRITE(undriven_34), .Q(membit_80_q));
  MUX1_16 mux1_16_5 (
    .d0(membit_65_q), .d1(membit_66_q), .d2(membit_67_q), .d3(membit_68_q), .d4(membit_69_q),
    .d5(membit_70_q), .d6(membit_71_q), .d7(membit_72_q), .d8(membit_73_q), .d9(membit_74_q),
    .d10(membit_75_q), .d11(membit_76_q), .d12(membit_77_q), .d13(membit_78_q), .d14(membit_79_q),
    .d15(membit_80_q), .s0(undriven_35), .s1(undriven_33), .s2(undriven_32), .s3(undriven_31),
    .s4(undriven_30), .s5(undriven_29), .s6(undriven_28), .s7(undriven_27), .s8(undriven_26),
    .s9(undriven_25), .s10(undriven_24), .s11(undriven_23), .s12(undriven_22), .s13(undriven_21),
    .s14(undriven_20), .s15(undriven_19), .Y(Q4));
  MEMBIT membit_81 (.D(D5), .WRITE(and_1_out), .Q(membit_81_q));
  MEMBIT membit_82 (.D(D5), .WRITE(and_2_out), .Q(membit_82_q));
  MEMBIT membit_83 (.D(D5), .WRITE(and_3_out), .Q(membit_83_q));
  MEMBIT membit_84 (.D(D5), .WRITE(and_4_out), .Q(membit_84_q));
  MEMBIT membit_85 (.D(D5), .WRITE(and_5_out), .Q(membit_85_q));
  MEMBIT membit_86 (.D(D5), .WRITE(and_6_out), .Q(membit_86_q));
  MEMBIT membit_87 (.D(D5), .WRITE(and_7_out), .Q(membit_87_q));
  MEMBIT membit_88 (.D(D5), .WRITE(and_8_out), .Q(membit_88_q));
  MEMBIT membit_89 (.D(D5), .WRITE(and_9_out), .Q(membit_89_q));
  MEMBIT membit_90 (.D(D5), .WRITE(and_10_out), .Q(membit_90_q));
  MEMBIT membit_91 (.D(D5), .WRITE(and_11_out), .Q(membit_91_q));
  MEMBIT membit_92 (.D(D5), .WRITE(and_12_out), .Q(membit_92_q));
  MEMBIT membit_93 (.D(D5), .WRITE(and_13_out), .Q(membit_93_q));
  MEMBIT membit_94 (.D(D5), .WRITE(and_14_out), .Q(membit_94_q));
  MEMBIT membit_95 (.D(D5), .WRITE(and_15_out), .Q(membit_95_q));
  MEMBIT membit_96 (.D(D5), .WRITE(undriven_34), .Q(membit_96_q));
  MUX1_16 mux1_16_6 (
    .d0(membit_81_q), .d1(membit_82_q), .d2(membit_83_q), .d3(membit_84_q), .d4(membit_85_q),
    .d5(membit_86_q), .d6(membit_87_q), .d7(membit_88_q), .d8(membit_89_q), .d9(membit_90_q),
    .d10(membit_91_q), .d11(membit_92_q), .d12(membit_93_q), .d13(membit_94_q), .d14(membit_95_q),
    .d15(membit_96_q), .s0(undriven_35), .s1(undriven_33), .s2(undriven_32), .s3(undriven_31),
    .s4(undriven_30), .s5(undriven_29), .s6(undriven_28), .s7(undriven_27), .s8(undriven_26),
    .s9(undriven_25), .s10(undriven_24), .s11(undriven_23), .s12(undriven_22), .s13(undriven_21),
    .s14(undriven_20), .s15(undriven_19), .Y(Q5));
  MEMBIT membit_97 (.D(D6), .WRITE(and_1_out), .Q(membit_97_q));
  MEMBIT membit_98 (.D(D6), .WRITE(and_2_out), .Q(membit_98_q));
  MEMBIT membit_99 (.D(D6), .WRITE(and_3_out), .Q(membit_99_q));
  MEMBIT membit_100 (.D(D6), .WRITE(and_4_out), .Q(membit_100_q));
  MEMBIT membit_101 (.D(D6), .WRITE(and_5_out), .Q(membit_101_q));
  MEMBIT membit_102 (.D(D6), .WRITE(and_6_out), .Q(membit_102_q));
  MEMBIT membit_103 (.D(D6), .WRITE(and_7_out), .Q(membit_103_q));
  MEMBIT membit_104 (.D(D6), .WRITE(and_8_out), .Q(membit_104_q));
  MEMBIT membit_105 (.D(D6), .WRITE(and_9_out), .Q(membit_105_q));
  MEMBIT membit_106 (.D(D6), .WRITE(and_10_out), .Q(membit_106_q));
  MEMBIT membit_107 (.D(D6), .WRITE(and_11_out), .Q(membit_107_q));
  MEMBIT membit_108 (.D(D6), .WRITE(and_12_out), .Q(membit_108_q));
  MEMBIT membit_109 (.D(D6), .WRITE(and_13_out), .Q(membit_109_q));
  MEMBIT membit_110 (.D(D6), .WRITE(and_14_out), .Q(membit_110_q));
  MEMBIT membit_111 (.D(D6), .WRITE(and_15_out), .Q(membit_111_q));
  MEMBIT membit_112 (.D(D6), .WRITE(undriven_34), .Q(membit_112_q));
  MUX1_16 mux1_16_7 (
    .d0(membit_97_q), .d1(membit_98_q), .d2(membit_99_q), .d3(membit_100_q), .d4(membit_101_q),
    .d5(membit_102_q), .d6(membit_103_q), .d7(membit_104_q), .d8(membit_105_q), .d9(membit_106_q),
    .d10(membit_107_q), .d11(membit_108_q), .d12(membit_109_q), .d13(membit_110_q), .d14(membit_111_q),
    .d15(membit_112_q), .s0(undriven_35), .s1(undriven_33), .s2(undriven_32), .s3(undriven_31),
    .s4(undriven_30), .s5(undriven_29), .s6(undriven_28), .s7(undriven_27), .s8(undriven_26),
    .s9(undriven_25), .s10(undriven_24), .s11(undriven_23), .s12(undriven_22), .s13(undriven_21),
    .s14(undriven_20), .s15(undriven_19), .Y(Q6));
  MEMBIT membit_113 (.D(D7), .WRITE(and_1_out), .Q(membit_113_q));
  MEMBIT membit_114 (.D(D7), .WRITE(and_2_out), .Q(membit_114_q));
  MEMBIT membit_115 (.D(D7), .WRITE(and_3_out), .Q(membit_115_q));
  MEMBIT membit_116 (.D(D7), .WRITE(and_4_out), .Q(membit_116_q));
  MEMBIT membit_117 (.D(D7), .WRITE(and_5_out), .Q(membit_117_q));
  MEMBIT membit_118 (.D(D7), .WRITE(and_6_out), .Q(membit_118_q));
  MEMBIT membit_119 (.D(D7), .WRITE(and_7_out), .Q(membit_119_q));
  MEMBIT membit_120 (.D(D7), .WRITE(and_8_out), .Q(membit_120_q));
  MEMBIT membit_121 (.D(D7), .WRITE(and_9_out), .Q(membit_121_q));
  MEMBIT membit_122 (.D(D7), .WRITE(and_10_out), .Q(membit_122_q));
  MEMBIT membit_123 (.D(D7), .WRITE(and_11_out), .Q(membit_123_q));
  MEMBIT membit_124 (.D(D7), .WRITE(and_12_out), .Q(membit_124_q));
  MEMBIT membit_125 (.D(D7), .WRITE(and_13_out), .Q(membit_125_q));
  MEMBIT membit_126 (.D(D7), .WRITE(and_14_out), .Q(membit_126_q));
  MEMBIT membit_127 (.D(D7), .WRITE(and_15_out), .Q(membit_127_q));
  MEMBIT membit_128 (.D(D7), .WRITE(undriven_34), .Q(membit_128_q));
  MUX1_16 mux1_16_8 (
    .d0(membit_113_q), .d1(membit_114_q), .d2(membit_115_q), .d3(membit_116_q), .d4(membit_117_q),
    .d5(membit_118_q), .d6(membit_119_q), .d7(membit_120_q), .d8(membit_121_q), .d9(membit_122_q),
    .d10(membit_123_q), .d11(membit_124_q), .d12(membit_125_q), .d13(membit_126_q), .d14(membit_127_q),
    .d15(membit_128_q), .s0(undriven_35), .s1(undriven_33), .s2(undriven_32), .s3(undriven_31),
    .s4(undriven_30), .s5(undriven_29), .s6(undriven_28), .s7(undriven_27), .s8(undriven_26),
    .s9(undriven_25), .s10(undriven_24), .s11(undriven_23), .s12(undriven_22), .s13(undriven_21),
    .s14(undriven_20), .s15(undriven_19), .Y(Q7));
  MEMBIT membit_129 (.D(D8), .WRITE(and_1_out), .Q(membit_129_q));
  MEMBIT membit_130 (.D(D8), .WRITE(and_2_out), .Q(membit_130_q));
  MEMBIT membit_131 (.D(D8), .WRITE(and_3_out), .Q(membit_131_q));
  MEMBIT membit_132 (.D(D8), .WRITE(and_4_out), .Q(membit_132_q));
  MEMBIT membit_133 (.D(D8), .WRITE(and_5_out), .Q(membit_133_q));
  MEMBIT membit_134 (.D(D8), .WRITE(and_6_out), .Q(membit_134_q));
  MEMBIT membit_135 (.D(D8), .WRITE(and_7_out), .Q(membit_135_q));
  MEMBIT membit_136 (.D(D8), .WRITE(and_8_out), .Q(membit_136_q));
  MEMBIT membit_137 (.D(D8), .WRITE(and_9_out), .Q(membit_137_q));
  MEMBIT membit_138 (.D(D8), .WRITE(and_10_out), .Q(membit_138_q));
  MEMBIT membit_139 (.D(D8), .WRITE(and_11_out), .Q(membit_139_q));
  MEMBIT membit_140 (.D(D8), .WRITE(and_12_out), .Q(membit_140_q));
  MEMBIT membit_141 (.D(D8), .WRITE(and_13_out), .Q(membit_141_q));
  MEMBIT membit_142 (.D(D8), .WRITE(and_14_out), .Q(membit_142_q));
  MEMBIT membit_143 (.D(D8), .WRITE(and_15_out), .Q(membit_143_q));
  MEMBIT membit_144 (.D(D8), .WRITE(undriven_34), .Q(membit_144_q));
  MUX1_16 mux1_16_9 (
    .d0(membit_129_q), .d1(membit_130_q), .d2(membit_131_q), .d3(membit_132_q), .d4(membit_133_q),
    .d5(membit_134_q), .d6(membit_135_q), .d7(membit_136_q), .d8(membit_137_q), .d9(membit_138_q),
    .d10(membit_139_q), .d11(membit_140_q), .d12(membit_141_q), .d13(membit_142_q), .d14(membit_143_q),
    .d15(membit_144_q), .s0(undriven_35), .s1(undriven_33), .s2(undriven_32), .s3(undriven_31),
    .s4(undriven_30), .s5(undriven_29), .s6(undriven_28), .s7(undriven_27), .s8(undriven_26),
    .s9(undriven_25), .s10(undriven_24), .s11(undriven_23), .s12(undriven_22), .s13(undriven_21),
    .s14(undriven_20), .s15(undriven_19), .Y(Q8));
  MEMBIT membit_145 (.D(D9), .WRITE(and_1_out), .Q(membit_145_q));
  MEMBIT membit_146 (.D(D9), .WRITE(and_2_out), .Q(membit_146_q));
  MEMBIT membit_147 (.D(D9), .WRITE(and_3_out), .Q(membit_147_q));
  MEMBIT membit_148 (.D(D9), .WRITE(and_4_out), .Q(membit_148_q));
  MEMBIT membit_149 (.D(D9), .WRITE(and_5_out), .Q(membit_149_q));
  MEMBIT membit_150 (.D(D9), .WRITE(and_6_out), .Q(membit_150_q));
  MEMBIT membit_151 (.D(D9), .WRITE(and_7_out), .Q(membit_151_q));
  MEMBIT membit_152 (.D(D9), .WRITE(and_8_out), .Q(membit_152_q));
  MEMBIT membit_153 (.D(D9), .WRITE(and_9_out), .Q(membit_153_q));
  MEMBIT membit_154 (.D(D9), .WRITE(and_10_out), .Q(membit_154_q));
  MEMBIT membit_155 (.D(D9), .WRITE(and_11_out), .Q(membit_155_q));
  MEMBIT membit_156 (.D(D9), .WRITE(and_12_out), .Q(membit_156_q));
  MEMBIT membit_157 (.D(D9), .WRITE(and_13_out), .Q(membit_157_q));
  MEMBIT membit_158 (.D(D9), .WRITE(and_14_out), .Q(membit_158_q));
  MEMBIT membit_159 (.D(D9), .WRITE(and_15_out), .Q(membit_159_q));
  MEMBIT membit_160 (.D(D9), .WRITE(undriven_34), .Q(membit_160_q));
  MUX1_16 mux1_16_10 (
    .d0(membit_145_q), .d1(membit_146_q), .d2(membit_147_q), .d3(membit_148_q), .d4(membit_149_q),
    .d5(membit_150_q), .d6(membit_151_q), .d7(membit_152_q), .d8(membit_153_q), .d9(membit_154_q),
    .d10(membit_155_q), .d11(membit_156_q), .d12(membit_157_q), .d13(membit_158_q), .d14(membit_159_q),
    .d15(membit_160_q), .s0(undriven_35), .s1(undriven_33), .s2(undriven_32), .s3(undriven_31),
    .s4(undriven_30), .s5(undriven_29), .s6(undriven_28), .s7(undriven_27), .s8(undriven_26),
    .s9(undriven_25), .s10(undriven_24), .s11(undriven_23), .s12(undriven_22), .s13(undriven_21),
    .s14(undriven_20), .s15(undriven_19), .Y(Q9));
  MEMBIT membit_161 (.D(D10), .WRITE(and_1_out), .Q(membit_161_q));
  MEMBIT membit_162 (.D(D10), .WRITE(and_2_out), .Q(membit_162_q));
  MEMBIT membit_163 (.D(D10), .WRITE(and_3_out), .Q(membit_163_q));
  MEMBIT membit_164 (.D(D10), .WRITE(and_4_out), .Q(membit_164_q));
  MEMBIT membit_165 (.D(D10), .WRITE(and_5_out), .Q(membit_165_q));
  MEMBIT membit_166 (.D(D10), .WRITE(and_6_out), .Q(membit_166_q));
  MEMBIT membit_167 (.D(D10), .WRITE(and_7_out), .Q(membit_167_q));
  MEMBIT membit_168 (.D(D10), .WRITE(and_8_out), .Q(membit_168_q));
  MEMBIT membit_169 (.D(D10), .WRITE(and_9_out), .Q(membit_169_q));
  MEMBIT membit_170 (.D(D10), .WRITE(and_10_out), .Q(membit_170_q));
  MEMBIT membit_171 (.D(D10), .WRITE(and_11_out), .Q(membit_171_q));
  MEMBIT membit_172 (.D(D10), .WRITE(and_12_out), .Q(membit_172_q));
  MEMBIT membit_173 (.D(D10), .WRITE(and_13_out), .Q(membit_173_q));
  MEMBIT membit_174 (.D(D10), .WRITE(and_14_out), .Q(membit_174_q));
  MEMBIT membit_175 (.D(D10), .WRITE(and_15_out), .Q(membit_175_q));
  MEMBIT membit_176 (.D(D10), .WRITE(undriven_34), .Q(membit_176_q));
  MUX1_16 mux1_16_11 (
    .d0(membit_161_q), .d1(membit_162_q), .d2(membit_163_q), .d3(membit_164_q), .d4(membit_165_q),
    .d5(membit_166_q), .d6(membit_167_q), .d7(membit_168_q), .d8(membit_169_q), .d9(membit_170_q),
    .d10(membit_171_q), .d11(membit_172_q), .d12(membit_173_q), .d13(membit_174_q), .d14(membit_175_q),
    .d15(membit_176_q), .s0(undriven_35), .s1(undriven_33), .s2(undriven_32), .s3(undriven_31),
    .s4(undriven_30), .s5(undriven_29), .s6(undriven_28), .s7(undriven_27), .s8(undriven_26),
    .s9(undriven_25), .s10(undriven_24), .s11(undriven_23), .s12(undriven_22), .s13(undriven_21),
    .s14(undriven_20), .s15(undriven_19), .Y(Q10));
  MEMBIT membit_177 (.D(D11), .WRITE(and_1_out), .Q(membit_177_q));
  MEMBIT membit_178 (.D(D11), .WRITE(and_2_out), .Q(membit_178_q));
  MEMBIT membit_179 (.D(D11), .WRITE(and_3_out), .Q(membit_179_q));
  MEMBIT membit_180 (.D(D11), .WRITE(and_4_out), .Q(membit_180_q));
  MEMBIT membit_181 (.D(D11), .WRITE(and_5_out), .Q(membit_181_q));
  MEMBIT membit_182 (.D(D11), .WRITE(and_6_out), .Q(membit_182_q));
  MEMBIT membit_183 (.D(D11), .WRITE(and_7_out), .Q(membit_183_q));
  MEMBIT membit_184 (.D(D11), .WRITE(and_8_out), .Q(membit_184_q));
  MEMBIT membit_185 (.D(D11), .WRITE(and_9_out), .Q(membit_185_q));
  MEMBIT membit_186 (.D(D11), .WRITE(and_10_out), .Q(membit_186_q));
  MEMBIT membit_187 (.D(D11), .WRITE(and_11_out), .Q(membit_187_q));
  MEMBIT membit_188 (.D(D11), .WRITE(and_12_out), .Q(membit_188_q));
  MEMBIT membit_189 (.D(D11), .WRITE(and_13_out), .Q(membit_189_q));
  MEMBIT membit_190 (.D(D11), .WRITE(and_14_out), .Q(membit_190_q));
  MEMBIT membit_191 (.D(D11), .WRITE(and_15_out), .Q(membit_191_q));
  MEMBIT membit_192 (.D(D11), .WRITE(undriven_34), .Q(membit_192_q));
  MUX1_16 mux1_16_12 (
    .d0(membit_177_q), .d1(membit_178_q), .d2(membit_179_q), .d3(membit_180_q), .d4(membit_181_q),
    .d5(membit_182_q), .d6(membit_183_q), .d7(membit_184_q), .d8(membit_185_q), .d9(membit_186_q),
    .d10(membit_187_q), .d11(membit_188_q), .d12(membit_189_q), .d13(membit_190_q), .d14(membit_191_q),
    .d15(membit_192_q), .s0(undriven_35), .s1(undriven_33), .s2(undriven_32), .s3(undriven_31),
    .s4(undriven_30), .s5(undriven_29), .s6(undriven_28), .s7(undriven_27), .s8(undriven_26),
    .s9(undriven_25), .s10(undriven_24), .s11(undriven_23), .s12(undriven_22), .s13(undriven_21),
    .s14(undriven_20), .s15(undriven_19), .Y(Q11));
  MEMBIT membit_193 (.D(D12), .WRITE(and_1_out), .Q(membit_193_q));
  MEMBIT membit_194 (.D(D12), .WRITE(and_2_out), .Q(membit_194_q));
  MEMBIT membit_195 (.D(D12), .WRITE(and_3_out), .Q(membit_195_q));
  MEMBIT membit_196 (.D(D12), .WRITE(and_4_out), .Q(membit_196_q));
  MEMBIT membit_197 (.D(D12), .WRITE(and_5_out), .Q(membit_197_q));
  MEMBIT membit_198 (.D(D12), .WRITE(and_6_out), .Q(membit_198_q));
  MEMBIT membit_199 (.D(D12), .WRITE(and_7_out), .Q(membit_199_q));
  MEMBIT membit_200 (.D(D12), .WRITE(and_8_out), .Q(membit_200_q));
  MEMBIT membit_201 (.D(D12), .WRITE(and_9_out), .Q(membit_201_q));
  MEMBIT membit_202 (.D(D12), .WRITE(and_10_out), .Q(membit_202_q));
  MEMBIT membit_203 (.D(D12), .WRITE(and_11_out), .Q(membit_203_q));
  MEMBIT membit_204 (.D(D12), .WRITE(and_12_out), .Q(membit_204_q));
  MEMBIT membit_205 (.D(D12), .WRITE(and_13_out), .Q(membit_205_q));
  MEMBIT membit_206 (.D(D12), .WRITE(and_14_out), .Q(membit_206_q));
  MEMBIT membit_207 (.D(D12), .WRITE(and_15_out), .Q(membit_207_q));
  MEMBIT membit_208 (.D(D12), .WRITE(undriven_34), .Q(membit_208_q));
  MUX1_16 mux1_16_13 (
    .d0(membit_193_q), .d1(membit_194_q), .d2(membit_195_q), .d3(membit_196_q), .d4(membit_197_q),
    .d5(membit_198_q), .d6(membit_199_q), .d7(membit_200_q), .d8(membit_201_q), .d9(membit_202_q),
    .d10(membit_203_q), .d11(membit_204_q), .d12(membit_205_q), .d13(membit_206_q), .d14(membit_207_q),
    .d15(membit_208_q), .s0(undriven_35), .s1(undriven_33), .s2(undriven_32), .s3(undriven_31),
    .s4(undriven_30), .s5(undriven_29), .s6(undriven_28), .s7(undriven_27), .s8(undriven_26),
    .s9(undriven_25), .s10(undriven_24), .s11(undriven_23), .s12(undriven_22), .s13(undriven_21),
    .s14(undriven_20), .s15(undriven_19), .Y(Q12));
  MEMBIT membit_209 (.D(D13), .WRITE(and_1_out), .Q(membit_209_q));
  MEMBIT membit_210 (.D(D13), .WRITE(and_2_out), .Q(membit_210_q));
  MEMBIT membit_211 (.D(D13), .WRITE(and_3_out), .Q(membit_211_q));
  MEMBIT membit_212 (.D(D13), .WRITE(and_4_out), .Q(membit_212_q));
  MEMBIT membit_213 (.D(D13), .WRITE(and_5_out), .Q(membit_213_q));
  MEMBIT membit_214 (.D(D13), .WRITE(and_6_out), .Q(membit_214_q));
  MEMBIT membit_215 (.D(D13), .WRITE(and_7_out), .Q(membit_215_q));
  MEMBIT membit_216 (.D(D13), .WRITE(and_8_out), .Q(membit_216_q));
  MEMBIT membit_217 (.D(D13), .WRITE(and_9_out), .Q(membit_217_q));
  MEMBIT membit_218 (.D(D13), .WRITE(and_10_out), .Q(membit_218_q));
  MEMBIT membit_219 (.D(D13), .WRITE(and_11_out), .Q(membit_219_q));
  MEMBIT membit_220 (.D(D13), .WRITE(and_12_out), .Q(membit_220_q));
  MEMBIT membit_221 (.D(D13), .WRITE(and_13_out), .Q(membit_221_q));
  MEMBIT membit_222 (.D(D13), .WRITE(and_14_out), .Q(membit_222_q));
  MEMBIT membit_223 (.D(D13), .WRITE(and_15_out), .Q(membit_223_q));
  MEMBIT membit_224 (.D(D13), .WRITE(undriven_34), .Q(membit_224_q));
  MUX1_16 mux1_16_14 (
    .d0(membit_209_q), .d1(membit_210_q), .d2(membit_211_q), .d3(membit_212_q), .d4(membit_213_q),
    .d5(membit_214_q), .d6(membit_215_q), .d7(membit_216_q), .d8(membit_217_q), .d9(membit_218_q),
    .d10(membit_219_q), .d11(membit_220_q), .d12(membit_221_q), .d13(membit_222_q), .d14(membit_223_q),
    .d15(membit_224_q), .s0(undriven_35), .s1(undriven_33), .s2(undriven_32), .s3(undriven_31),
    .s4(undriven_30), .s5(undriven_29), .s6(undriven_28), .s7(undriven_27), .s8(undriven_26),
    .s9(undriven_25), .s10(undriven_24), .s11(undriven_23), .s12(undriven_22), .s13(undriven_21),
    .s14(undriven_20), .s15(undriven_19), .Y(Q13));
  MEMBIT membit_225 (.D(D14), .WRITE(and_1_out), .Q(membit_225_q));
  MEMBIT membit_226 (.D(D14), .WRITE(and_2_out), .Q(membit_226_q));
  MEMBIT membit_227 (.D(D14), .WRITE(and_3_out), .Q(membit_227_q));
  MEMBIT membit_228 (.D(D14), .WRITE(and_4_out), .Q(membit_228_q));
  MEMBIT membit_229 (.D(D14), .WRITE(and_5_out), .Q(membit_229_q));
  MEMBIT membit_230 (.D(D14), .WRITE(and_6_out), .Q(membit_230_q));
  MEMBIT membit_231 (.D(D14), .WRITE(and_7_out), .Q(membit_231_q));
  MEMBIT membit_232 (.D(D14), .WRITE(and_8_out), .Q(membit_232_q));
  MEMBIT membit_233 (.D(D14), .WRITE(and_9_out), .Q(membit_233_q));
  MEMBIT membit_234 (.D(D14), .WRITE(and_10_out), .Q(membit_234_q));
  MEMBIT membit_235 (.D(D14), .WRITE(and_11_out), .Q(membit_235_q));
  MEMBIT membit_236 (.D(D14), .WRITE(and_12_out), .Q(membit_236_q));
  MEMBIT membit_237 (.D(D14), .WRITE(and_13_out), .Q(membit_237_q));
  MEMBIT membit_238 (.D(D14), .WRITE(and_14_out), .Q(membit_238_q));
  MEMBIT membit_239 (.D(D14), .WRITE(and_15_out), .Q(membit_239_q));
  MEMBIT membit_240 (.D(D14), .WRITE(undriven_34), .Q(membit_240_q));
  MUX1_16 mux1_16_15 (
    .d0(membit_225_q), .d1(membit_226_q), .d2(membit_227_q), .d3(membit_228_q), .d4(membit_229_q),
    .d5(membit_230_q), .d6(membit_231_q), .d7(membit_232_q), .d8(membit_233_q), .d9(membit_234_q),
    .d10(membit_235_q), .d11(membit_236_q), .d12(membit_237_q), .d13(membit_238_q), .d14(membit_239_q),
    .d15(membit_240_q), .s0(undriven_35), .s1(undriven_33), .s2(undriven_32), .s3(undriven_31),
    .s4(undriven_30), .s5(undriven_29), .s6(undriven_28), .s7(undriven_27), .s8(undriven_26),
    .s9(undriven_25), .s10(undriven_24), .s11(undriven_23), .s12(undriven_22), .s13(undriven_21),
    .s14(undriven_20), .s15(undriven_19), .Y(Q14));
  MEMBIT membit_241 (.D(D15), .WRITE(and_1_out), .Q(membit_241_q));
  MEMBIT membit_242 (.D(D15), .WRITE(and_2_out), .Q(membit_242_q));
  MEMBIT membit_243 (.D(D15), .WRITE(and_3_out), .Q(membit_243_q));
  MEMBIT membit_244 (.D(D15), .WRITE(and_4_out), .Q(membit_244_q));
  MEMBIT membit_245 (.D(D15), .WRITE(and_5_out), .Q(membit_245_q));
  MEMBIT membit_246 (.D(D15), .WRITE(and_6_out), .Q(membit_246_q));
  MEMBIT membit_247 (.D(D15), .WRITE(and_7_out), .Q(membit_247_q));
  MEMBIT membit_248 (.D(D15), .WRITE(and_8_out), .Q(membit_248_q));
  MEMBIT membit_249 (.D(D15), .WRITE(and_9_out), .Q(membit_249_q));
  MEMBIT membit_250 (.D(D15), .WRITE(and_10_out), .Q(membit_250_q));
  MEMBIT membit_251 (.D(D15), .WRITE(and_11_out), .Q(membit_251_q));
  MEMBIT membit_252 (.D(D15), .WRITE(and_12_out), .Q(membit_252_q));
  MEMBIT membit_253 (.D(D15), .WRITE(and_13_out), .Q(membit_253_q));
  MEMBIT membit_254 (.D(D15), .WRITE(and_14_out), .Q(membit_254_q));
  MEMBIT membit_255 (.D(D15), .WRITE(and_15_out), .Q(membit_255_q));
  MEMBIT membit_256 (.D(D15), .WRITE(undriven_34), .Q(membit_256_q));
  MUX1_16 mux1_16_16 (
    .d0(membit_241_q), .d1(membit_242_q), .d2(membit_243_q), .d3(membit_244_q), .d4(membit_245_q),
    .d5(membit_246_q), .d6(membit_247_q), .d7(membit_248_q), .d8(membit_249_q), .d9(membit_250_q),
    .d10(membit_251_q), .d11(membit_252_q), .d12(membit_253_q), .d13(membit_254_q), .d14(membit_255_q),
    .d15(membit_256_q), .s0(undriven_35), .s1(undriven_33), .s2(undriven_32), .s3(undriven_31),
    .s4(undriven_30), .s5(undriven_29), .s6(undriven_28), .s7(undriven_27), .s8(undriven_26),
    .s9(undriven_25), .s10(undriven_24), .s11(undriven_23), .s12(undriven_22), .s13(undriven_21),
    .s14(undriven_20), .s15(undriven_19), .Y(Q15));
endmodule

module AND3 (
  input  A,
  input  B,
  input  C,
  output Y
);

  wire and_1_y;

  AND and_1 (.A(A), .B(B), .Y(and_1_y));
  AND and_2 (.A(and_1_y), .B(C), .Y(Y));
endmodule

module XNOR (
  input  A,
  input  B,
  output Y
);

  wire xor_1_y;

  XOR xor_1 (.A(A), .B(B), .Y(xor_1_y));
  NOT not_1 (.A(xor_1_y), .Y(Y));
endmodule

module HALFADD (
  input  A,
  input  B,
  output S,
  output C
);

  wire undriven, undriven_2;

  XOR xor_1 (.A(A), .B(B), .Y(S));
  AND and_1 (.A(undriven), .B(undriven_2), .Y(C));
endmodule

module DECODER3 (
  input  S0,
  input  S1,
  input  S2,
  output D0,
  output D1,
  output D2,
  output D3,
  output D4,
  output D5,
  output D6,
  output D7
);

  wire not_1_y, not_2_y, not_3_y, undriven, undriven_2, undriven_3, undriven_4, undriven_5, undriven_6,
       undriven_7, undriven_8, undriven_9, undriven_10, undriven_11, undriven_12, undriven_13, undriven_14,
       undriven_15, undriven_16, undriven_17, undriven_18, undriven_19, undriven_20, undriven_21;

  NOT not_1 (.A(S0), .Y(not_1_y));
  NOT not_2 (.A(S1), .Y(not_2_y));
  NOT not_3 (.A(S2), .Y(not_3_y));
  AND3 and3_1 (.A(undriven), .B(undriven_2), .C(undriven_3), .Y(D0));
  AND3 and3_2 (.A(undriven_4), .B(undriven_5), .C(undriven_6), .Y(D1));
  AND3 and3_3 (.A(undriven_7), .B(undriven_8), .C(undriven_9), .Y(D2));
  AND3 and3_4 (.A(undriven_10), .B(undriven_11), .C(not_3_y), .Y(D3));
  AND3 and3_5 (.A(undriven_12), .B(undriven_13), .C(undriven_14), .Y(D4));
  AND3 and3_6 (.A(undriven_15), .B(not_2_y), .C(undriven_16), .Y(D5));
  AND3 and3_7 (.A(not_1_y), .B(undriven_17), .C(undriven_18), .Y(D6));
  AND3 and3_8 (.A(undriven_19), .B(undriven_20), .C(undriven_21), .Y(D7));
endmodule

module DEMUX3 (
  input  S0,
  input  S1,
  input  S2,
  input  X,
  output Y0,
  output Y1,
  output Y2,
  output Y3,
  output Y4,
  output Y5,
  output Y6,
  output Y7
);

  wire decoder3_1_d0, decoder3_1_d1, decoder3_1_d2, decoder3_1_d3, decoder3_1_d4, decoder3_1_d5,
       decoder3_1_d6, decoder3_1_d7, undriven, undriven_2, undriven_3, undriven_4, undriven_5, undriven_6,
       undriven_7;

  DECODER3 decoder3_1 (
    .S0(S0), .S1(S1), .S2(S2), .D0(decoder3_1_d0), .D1(decoder3_1_d1), .D2(decoder3_1_d2),
    .D3(decoder3_1_d3), .D4(decoder3_1_d4), .D5(decoder3_1_d5), .D6(decoder3_1_d6), .D7(decoder3_1_d7));
  AND and_1 (.A(decoder3_1_d0), .B(X), .Y(Y0));
  AND and_2 (.A(decoder3_1_d1), .B(undriven), .Y(Y1));
  AND and_3 (.A(decoder3_1_d2), .B(undriven_2), .Y(Y2));
  AND and_4 (.A(decoder3_1_d3), .B(undriven_3), .Y(Y3));
  AND and_5 (.A(decoder3_1_d4), .B(undriven_4), .Y(Y4));
  AND and_6 (.A(decoder3_1_d5), .B(undriven_5), .Y(Y5));
  AND and_7 (.A(decoder3_1_d6), .B(undriven_6), .Y(Y6));
  AND and_8 (.A(decoder3_1_d7), .B(undriven_7), .Y(Y7));
endmodule

module MUX1_8 (
  input  d0,
  input  d1,
  input  d2,
  input  d3,
  input  d4,
  input  d5,
  input  d6,
  input  d7,
  input  s0,
  input  s1,
  input  s2,
  input  s3,
  input  s4,
  input  s5,
  input  s6,
  input  s7,
  output Y
);

  wire and_1_out, and_2_out, and_3_out, and_4_out, and_5_out, and_6_out, and_7_out, and_8_out, or_1_out,
       or_2_out, or_3_out, or_4_out, or_5_out, or_6_out;

  and and_1 (and_1_out, d0, s0);
  and and_2 (and_2_out, d1, s1);
  and and_3 (and_3_out, d2, s2);
  and and_4 (and_4_out, d3, s3);
  and and_5 (and_5_out, d4, s4);
  and and_6 (and_6_out, d5, s5);
  and and_7 (and_7_out, d6, s6);
  and and_8 (and_8_out, d7, s7);
  or or_1 (or_1_out, and_1_out, and_2_out);
  or or_2 (or_2_out, and_3_out, and_4_out);
  or or_3 (or_3_out, and_5_out, and_6_out);
  or or_4 (or_4_out, and_7_out, and_8_out);
  or or_5 (or_5_out, or_1_out, or_2_out);
  or or_6 (or_6_out, or_3_out, or_4_out);
  or or_7 (Y, or_5_out, or_6_out);
endmodule

module ALU16B (
  input  OP0,
  input  OP1,
  input  OP2,
  input  [15:0] A,
  input  [15:0] B,
  output Zero,
  output Pos,
  output [15:0] R
);

  wire add16b_1_p1, notb_1_y, notb_2_y, notb_3_y, notb_4_y, notb_5_y, notb_6_y, notb_7_y, notb_8_y, notb_9_y,
       notb_10_y, notb_11_y, notb_12_y, notb_13_y, notb_14_y, notb_15_y, notb_16_y, notb_18_y, notb_19_y,
       or16b_1_y, undriven, undriven_2, undriven_3, undriven_4, undriven_5, undriven_6, undriven_7,
       undriven_8, undriven_9, undriven_10, undriven_11, undriven_12, undriven_13, undriven_14, undriven_15,
       undriven_16, undriven_17, undriven_18, undriven_19, undriven_20, undriven_21, undriven_22,
       undriven_23, undriven_24, undriven_25, undriven_26, undriven_27, undriven_28, undriven_29,
       undriven_30, undriven_31, undriven_32;
  wire [15:0] add16b_1_p35, add16b_2_s0, and16b_1_y0, and_1_out, and_2_out, and_3_out, and_4_out, and_5_out,
       and_6_out, and_7_out, decoder3_1_d0, decoder3_1_d2, decoder3_1_d4, decoder3_1_d6, lshift16b_1_y0,
       or_1_out, or_2_out, or_3_out, or_4_out, or_5_out, rshift16b_1_y0, xor16b_1_y0;
  wire [15:15] decoder3_1_d1, decoder3_1_d3, decoder3_1_d5;

  DECODER3 decoder3_1 (
    .S0(OP0), .S1(OP1), .S2(OP2), .D0(decoder3_1_d0[0]), .D1(decoder3_1_d1[15]), .D2(decoder3_1_d2[0]),
    .D3(decoder3_1_d3[15]), .D4(decoder3_1_d4[0]), .D5(decoder3_1_d5[15]), .D6(decoder3_1_d6[0]));  // open: D7
  NOTB notb_1 (.A(B[0]), .Y(notb_1_y));
  NOTB notb_2 (.A(B[1]), .Y(notb_2_y));
  NOTB notb_3 (.A(B[2]), .Y(notb_3_y));
  NOTB notb_4 (.A(B[3]), .Y(notb_4_y));
  NOTB notb_5 (.A(B[4]), .Y(notb_5_y));
  NOTB notb_6 (.A(B[5]), .Y(notb_6_y));
  NOTB notb_7 (.A(B[6]), .Y(notb_7_y));
  NOTB notb_8 (.A(B[7]), .Y(notb_8_y));
  NOTB notb_9 (.A(B[8]), .Y(notb_9_y));
  NOTB notb_10 (.A(B[9]), .Y(notb_10_y));
  NOTB notb_11 (.A(B[10]), .Y(notb_11_y));
  NOTB notb_12 (.A(B[11]), .Y(notb_12_y));
  NOTB notb_13 (.A(B[12]), .Y(notb_13_y));
  NOTB notb_14 (.A(B[13]), .Y(notb_14_y));
  NOTB notb_15 (.A(B[14]), .Y(notb_15_y));
  NOTB notb_16 (.A(B[15]), .Y(notb_16_y));
  // ADD16B add16b_1: pin names not known; wires that end beside it: add16b_1_p1, A[0], A[1], A[2], A[3], A[4], A[5], A[6], A[7], A[8], A[9], A[10], A[11], A[12], A[13], A[14], A[15], B[0], B[1], B[2], B[3], B[4], B[5], B[6], B[7], B[8], B[9], B[10], B[11], B[12], B[13], B[14], B[15], 1'b0, add16b_1_p35[0], add16b_1_p35[1], add16b_1_p35[2], add16b_1_p35[3], add16b_1_p35[4], add16b_1_p35[5], add16b_1_p35[6], add16b_1_p35[7], add16b_1_p35[8], add16b_1_p35[9], add16b_1_p35[10], add16b_1_p35[11], add16b_1_p35[12], add16b_1_p35[13], add16b_1_p35[14], add16b_1_p35[15]
  ADD16B add16b_2 (
    .A0(add16b_1_p1), .A1(A[1]), .A2(A[2]), .A3(A[3]), .A4(A[4]), .A5(A[5]), .A6(A[6]), .A7(A[7]), .A8(A[8]),
    .A9(A[9]), .A10(A[10]), .A11(A[11]), .A12(A[12]), .A13(A[13]), .A14(A[14]), .A15(A[15]), .B0(notb_1_y),
    .B1(notb_2_y), .B2(notb_3_y), .B3(notb_4_y), .B4(notb_5_y), .B5(notb_6_y), .B6(notb_7_y), .B7(notb_8_y),
    .B8(notb_9_y), .B9(notb_10_y), .B10(notb_11_y), .B11(notb_12_y), .B12(notb_13_y), .B13(notb_14_y),
    .B14(notb_15_y), .B15(notb_16_y), .Cin(1'b1), .S0(add16b_2_s0[0]), .S1(add16b_2_s0[1]),
    .S2(add16b_2_s0[2]), .S3(add16b_2_s0[3]), .S4(add16b_2_s0[4]), .S5(add16b_2_s0[5]), .S6(add16b_2_s0[6]),
    .S7(add16b_2_s0[7]), .S8(add16b_2_s0[8]), .S9(add16b_2_s0[9]), .S10(add16b_2_s0[10]),
    .S11(add16b_2_s0[11]), .S12(add16b_2_s0[12]), .S13(add16b_2_s0[13]), .S14(add16b_2_s0[14]),
    .S15(add16b_2_s0[15]));  // open: Cout
  AND16B and16b_1 (
    .A0(add16b_1_p1), .A1(A[1]), .A2(A[2]), .A3(A[3]), .A4(A[4]), .A5(A[5]), .A6(A[6]), .A7(A[7]), .A8(A[8]),
    .A9(A[9]), .A10(A[10]), .A11(A[11]), .A12(A[12]), .A13(A[13]), .A14(A[14]), .A15(A[15]),
    .B0(undriven_11), .B1(undriven_10), .B2(undriven_12), .B3(undriven_9), .B4(undriven_8), .B5(undriven_13),
    .B6(undriven_7), .B7(undriven_6), .B8(undriven_14), .B9(undriven_5), .B10(undriven_4), .B11(undriven_15),
    .B12(undriven_3), .B13(undriven_2), .B14(undriven_17), .B15(undriven), .Y0(and16b_1_y0[0]),
    .Y1(and16b_1_y0[1]), .Y2(and16b_1_y0[2]), .Y3(and16b_1_y0[3]), .Y4(and16b_1_y0[4]), .Y5(and16b_1_y0[5]),
    .Y6(and16b_1_y0[6]), .Y7(and16b_1_y0[7]), .Y8(and16b_1_y0[8]), .Y9(and16b_1_y0[9]),
    .Y10(and16b_1_y0[10]), .Y11(and16b_1_y0[11]), .Y12(and16b_1_y0[12]), .Y13(and16b_1_y0[13]),
    .Y14(and16b_1_y0[14]), .Y15(and16b_1_y0[15]));
  XOR16B xor16b_1 (
    .A0(add16b_1_p1), .A1(A[1]), .A2(A[2]), .A3(A[3]), .A4(A[4]), .A5(A[5]), .A6(A[6]), .A7(A[7]), .A8(A[8]),
    .A9(A[9]), .A10(A[10]), .A11(A[11]), .A12(A[12]), .A13(A[13]), .A14(A[14]), .A15(A[15]),
    .B0(undriven_32), .B1(undriven_31), .B2(undriven_30), .B3(undriven_29), .B4(undriven_28),
    .B5(undriven_27), .B6(undriven_26), .B7(undriven_25), .B8(undriven_24), .B9(undriven_23),
    .B10(undriven_22), .B11(undriven_16), .B12(undriven_21), .B13(undriven_20), .B14(undriven_18),
    .B15(undriven_19), .Y0(xor16b_1_y0[0]), .Y1(xor16b_1_y0[1]), .Y2(xor16b_1_y0[2]), .Y3(xor16b_1_y0[3]),
    .Y4(xor16b_1_y0[4]), .Y5(xor16b_1_y0[5]), .Y6(xor16b_1_y0[6]), .Y7(xor16b_1_y0[7]), .Y8(xor16b_1_y0[8]),
    .Y9(xor16b_1_y0[9]), .Y10(xor16b_1_y0[10]), .Y11(xor16b_1_y0[11]), .Y12(xor16b_1_y0[12]),
    .Y13(xor16b_1_y0[13]), .Y14(xor16b_1_y0[14]), .Y15(xor16b_1_y0[15]));
  LSHIFT16B lshift16b_1 (
    .A0(add16b_1_p1), .A1(A[1]), .A2(A[2]), .A3(A[3]), .A4(A[4]), .A5(A[5]), .A6(A[6]), .A7(A[7]), .A8(A[8]),
    .A9(A[9]), .A10(A[10]), .A11(A[11]), .A12(A[12]), .A13(A[13]), .A14(A[14]), .A15(A[15]),
    .N0(undriven_32), .N1(undriven_31), .N2(undriven_30), .N3(undriven_29), .Y0(lshift16b_1_y0[0]),
    .Y1(lshift16b_1_y0[1]), .Y2(lshift16b_1_y0[2]), .Y3(lshift16b_1_y0[3]), .Y4(lshift16b_1_y0[4]),
    .Y5(lshift16b_1_y0[5]), .Y6(lshift16b_1_y0[6]), .Y7(lshift16b_1_y0[7]), .Y8(lshift16b_1_y0[8]),
    .Y9(lshift16b_1_y0[9]), .Y10(lshift16b_1_y0[10]), .Y11(lshift16b_1_y0[11]), .Y12(lshift16b_1_y0[12]),
    .Y13(lshift16b_1_y0[13]), .Y14(lshift16b_1_y0[14]), .Y15(lshift16b_1_y0[15]));
  RSHIFT16B rshift16b_1 (
    .A0(add16b_1_p1), .A1(A[1]), .A2(A[2]), .A3(A[3]), .A4(A[4]), .A5(A[5]), .A6(A[6]), .A7(A[7]), .A8(A[8]),
    .A9(A[9]), .A10(A[10]), .A11(A[11]), .A12(A[12]), .A13(A[13]), .A14(A[14]), .A15(A[15]),
    .N0(undriven_32), .N1(undriven_31), .N2(undriven_30), .N3(undriven_29), .Y0(rshift16b_1_y0[0]),
    .Y1(rshift16b_1_y0[1]), .Y2(rshift16b_1_y0[2]), .Y3(rshift16b_1_y0[3]), .Y4(rshift16b_1_y0[4]),
    .Y5(rshift16b_1_y0[5]), .Y6(rshift16b_1_y0[6]), .Y7(rshift16b_1_y0[7]), .Y8(rshift16b_1_y0[8]),
    .Y9(rshift16b_1_y0[9]), .Y10(rshift16b_1_y0[10]), .Y11(rshift16b_1_y0[11]), .Y12(rshift16b_1_y0[12]),
    .Y13(rshift16b_1_y0[13]), .Y14(rshift16b_1_y0[14]), .Y15(rshift16b_1_y0[15]));
  assign and_1_out = add16b_1_p35 & decoder3_1_d0;  // AND_Gate and_1, 16 bits wide
  assign and_2_out = add16b_2_s0 & {16{decoder3_1_d1[15]}};  // AND_Gate and_2, 16 bits wide
  assign and_3_out = and16b_1_y0 & decoder3_1_d2;  // AND_Gate and_3, 16 bits wide
  assign and_4_out = xor16b_1_y0 & {16{decoder3_1_d3[15]}};  // AND_Gate and_4, 16 bits wide
  assign and_5_out = lshift16b_1_y0 & decoder3_1_d4;  // AND_Gate and_5, 16 bits wide
  assign and_6_out = rshift16b_1_y0 & {16{decoder3_1_d5[15]}};  // AND_Gate and_6, 16 bits wide
  assign and_7_out = B & decoder3_1_d6;  // AND_Gate and_7, 16 bits wide
  assign or_1_out = and_1_out | and_2_out;  // OR_Gate or_1, 16 bits wide
  assign or_2_out = and_3_out | and_4_out;  // OR_Gate or_2, 16 bits wide
  assign or_3_out = and_5_out | and_6_out;  // OR_Gate or_3, 16 bits wide
  assign or_4_out = or_1_out | or_2_out;  // OR_Gate or_4, 16 bits wide
  assign or_5_out = or_3_out | and_7_out;  // OR_Gate or_5, 16 bits wide
  assign R = or_4_out | or_5_out;  // OR_Gate or_6, 16 bits wide
  OR16B or16b_1 (
    .i0(R[0]), .i1(R[1]), .i2(R[2]), .i3(R[3]), .i4(R[4]), .i5(R[5]), .i6(R[6]), .i7(R[7]), .i8(R[8]),
    .i9(R[9]), .i10(R[10]), .i11(R[11]), .i12(R[12]), .i13(R[13]), .i14(R[14]), .i15(R[15]), .Y(or16b_1_y));
  NOTB notb_17 (.A(or16b_1_y), .Y(Zero));
  NOTB notb_18 (.A(R[15]), .Y(notb_18_y));
  NOTB notb_19 (.A(Zero), .Y(notb_19_y));
  and and_8 (Pos, notb_18_y, notb_19_y);
endmodule
